// Logisim project 4bitcpu.circ as structural Verilog
module main (
);

  wire clock_1_out, cpu_1_mem_write;
  wire [7:0] cpu_1_adress, cpu_1_memout, ram_1_data;

  Clock clock_1 (.out(clock_1_out));
  CPU cpu_1 (
    .MEMIN(ram_1_data), .CLCK(clock_1_out), .MEM_WRITE(cpu_1_mem_write), .MEMOUT(cpu_1_memout),
    .ADRESS(cpu_1_adress));
  RAM #(.bus("separate")) ram_1 (
    .addr(cpu_1_adress), .din(cpu_1_memout), .data(ram_1_data), .str(cpu_1_mem_write), .clk(clock_1_out));  // open: sel, ld, clr
endmodule

module CPU (
  input  [7:0] MEMIN,
  input  CLCK,
  output [7:0] MEMOUT,
  output MEM_WRITE,
  output [7:0] ADRESS
);

  wire CLR_out, decoder_1_out1, decoder_1_out2, decoder_1_out3, pipeline_1_count_plus_plus, pipeline_1_fetch,
       pipeline_1_move;
  wire [1:0] DEST, SRC;
  wire [3:0] A_q, alu_1_out, B_q, OPcode_q;

  Decoder #(.select(2), .disabled(0)) decoder_1 (
    .out0(MEM_WRITE), .out1(decoder_1_out1), .out2(decoder_1_out2), .out3(decoder_1_out3), .sel(DEST),
    .en(pipeline_1_move));
  Pipeline pipeline_1 (
    .CLOCK(CLCK), .FETCH(pipeline_1_fetch), .Count_plus_plus(pipeline_1_count_plus_plus),
    .MOVE(pipeline_1_move), .CLR(CLR_out));
  Register OPcode (.D(MEMIN), .en(pipeline_1_fetch), .Q({SRC, DEST, OPcode_q}), .clk(CLCK), .clr(CLR_out));
  Register #(.width(4)) A (.D(MEMOUT[3:0]), .en(decoder_1_out1), .Q(A_q), .clk(CLCK), .clr(CLR_out));
  Register #(.width(4)) B (.D(MEMOUT[3:0]), .en(decoder_1_out2), .Q(B_q), .clk(CLCK), .clr(CLR_out));
  Counter counter_1 (
    .load(decoder_1_out3), .D(MEMIN), .count(pipeline_1_count_plus_plus), .Q(ADRESS), .clk(CLCK),
    .clr(CLR_out));  // open: carry
  Button CLR (.out(CLR_out));
  ALU alu_1 (.A(A_q), .B(B_q), .in_3(OPcode_q), .OUT(alu_1_out));
  Multiplexer #(.select(2), .width(4), .enable("false")) multiplexer_1 (
    .in0(OPcode_q), .in1(A_q), .in2(B_q), .in3(alu_1_out), .out(MEMOUT[3:0]), .sel(SRC));

  assign MEMOUT[7:4] = MEMIN[7:4];

  // Other names for the same wires on the sheet: DATA[3:0] = MEMOUT[3:0]
endmodule

module Pipeline (
  input  CLOCK,
  input  CLR,
  output Count_plus_plus,
  output FETCH,
  output MOVE
);

  D_Flip_Flop d_ff_1 (.clk(CLOCK), .D(FETCH), .Q(MOVE), .Qn(FETCH), .reset(CLR));  // open: preset, en
  buf or_1 (Count_plus_plus, FETCH);  // OR_Gate
endmodule

module ALU (
  input  [3:0] A,
  input  [3:0] B,
  input  [3:0] in_3,
  output [3:0] OUT
);

  wire [3:0] adder_1_out;

  Adder #(.width(4)) adder_1 (.a(A), .b(B), .out(adder_1_out));  // open: cin, cout
  Multiplexer #(.select(4), .width(4), .enable("false")) multiplexer_1 (
    .in0(adder_1_out), .out(OUT), .sel(in_3));  // open: in1, in2, in3, in4, in5, in6, in7, in8, in9, in10, in11, in12, in13, in14, in15
endmodule
