// Logisim project roget_v3.circ as structural Verilog: 13 circuits, main circuit main
module main (
);

  wire ADDRESS_E, button_1_out, CHAR_AV, CHAR_E, CLCK, clock_1_out, CLR_SCREEN, CLR_SCREEN_MEM,
       cpu_1_mem_read, cpu_1_soft_interrupt, decoder_1_out0, decoder_1_out1, decoder_1_out2, or_1_out,
       or_3_out, or_5_out, P_O, P_V, POWER_ON, powerswitch_1_clck_out, RESET, RESET_C, RESET_out,
       TICK_TICK_BOOM_out, Trigger;
  wire [3:0] cpu_1_address_2;
  wire [6:0] CHAR, CHAR_IN;
  wire [7:0] cpu_1_address, cpu_1_data_out, DATA_R, demultiplexer_1_out0, demultiplexer_1_out2, KEY_IN,
       multiplexer_2_out, multiplexer_3_out, or_6_out, ram_1_data;
  wire [9:0] Coords;
  wire [15:0] ADDRESS_R, multiplexer_1_out;
  wire [15:12] cpu_1_address_3;
  wire [31:0] gpu_1_out_6, gpu_1_out_7, gpu_1_out_8, gpu_1_out_9, gpu_1_out_10, gpu_1_out_11, gpu_1_out_12,
       gpu_1_out_13, gpu_1_out_14, gpu_1_out_15, gpu_1_out_16, gpu_1_out_17, gpu_1_out_18, gpu_1_out_19,
       gpu_1_out_20, gpu_1_out_21, gpu_1_out_22, gpu_1_out_23, gpu_1_out_24, gpu_1_out_25, gpu_1_out_26,
       gpu_1_out_27, gpu_1_out_28, gpu_1_out_29, gpu_1_out_30, gpu_1_out_31, gpu_1_out_32, gpu_1_out_33,
       gpu_1_out_34, gpu_1_out_35, gpu_1_out_36, gpu_1_out_37;

  TTY #(.rows(32), .cols(64)) tty_1 (.data(CHAR), .clk(CLCK), .we(CHAR_E), .clr(or_1_out));
  or or_1 (or_1_out, RESET, CLR_SCREEN);
  LED led_1 (.in(P_O));
  Button u_POWER_ON (.out(POWER_ON));
  Keyboard keyboard_1 (.clk(CLCK), .clr(RESET), .avail(CHAR_AV), .data(CHAR_IN));  // open: re
  GPU gpu_1 (
    .out_6(gpu_1_out_6), .out_7(gpu_1_out_7), .out_8(gpu_1_out_8), .out_9(gpu_1_out_9),
    .out_10(gpu_1_out_10), .out_11(gpu_1_out_11), .out_12(gpu_1_out_12), .out_13(gpu_1_out_13),
    .out_14(gpu_1_out_14), .out_15(gpu_1_out_15), .out_16(gpu_1_out_16), .out_17(gpu_1_out_17),
    .out_18(gpu_1_out_18), .out_19(gpu_1_out_19), .out_20(gpu_1_out_20), .out_21(gpu_1_out_21),
    .out_22(gpu_1_out_22), .out_23(gpu_1_out_23), .out_24(gpu_1_out_24), .out_25(gpu_1_out_25),
    .out_26(gpu_1_out_26), .out_27(gpu_1_out_27), .out_28(gpu_1_out_28), .out_29(gpu_1_out_29),
    .out_30(gpu_1_out_30), .out_31(gpu_1_out_31), .out_32(gpu_1_out_32), .out_33(gpu_1_out_33),
    .out_34(gpu_1_out_34), .out_35(gpu_1_out_35), .out_36(gpu_1_out_36), .out_37(gpu_1_out_37),
    .SELECT_X(Coords[9:5]), .CLCK(Trigger), .CLR(or_3_out), .SELECT_Y(Coords[4:0]), .CLR_WRITE(P_V));
  DotMatrix #(.matrixcols(32), .matrixrows(32), .persist(1)) dotmatrix_1 (
    .col0(gpu_1_out_6), .col1(gpu_1_out_7), .col2(gpu_1_out_8), .col3(gpu_1_out_9), .col4(gpu_1_out_10),
    .col5(gpu_1_out_11), .col6(gpu_1_out_12), .col7(gpu_1_out_13), .col8(gpu_1_out_14), .col9(gpu_1_out_15),
    .col10(gpu_1_out_16), .col11(gpu_1_out_17), .col12(gpu_1_out_18), .col13(gpu_1_out_19),
    .col14(gpu_1_out_20), .col15(gpu_1_out_21), .col16(gpu_1_out_22), .col17(gpu_1_out_23),
    .col18(gpu_1_out_24), .col19(gpu_1_out_25), .col20(gpu_1_out_26), .col21(gpu_1_out_27),
    .col22(gpu_1_out_28), .col23(gpu_1_out_29), .col24(gpu_1_out_30), .col25(gpu_1_out_31),
    .col26(gpu_1_out_32), .col27(gpu_1_out_33), .col28(gpu_1_out_34), .col29(gpu_1_out_35),
    .col30(gpu_1_out_36), .col31(gpu_1_out_37));
  Button button_1 (.out(button_1_out));
  Clock clock_1 (.out(clock_1_out));
  Button TICK_TICK_BOOM (.out(TICK_TICK_BOOM_out));
  Button u_RESET (.out(RESET_out));
  or or_2 (RESET, RESET_out, RESET_C);
  Program_Loader program_loader_1 (
    .CLCK(CLCK), .WRITE(button_1_out), .RESET(RESET), .ADDRESS(ADDRESS_R), .WRITING(ADDRESS_E));
  or or_3 (or_3_out, RESET, CLR_SCREEN_MEM);
  Multiplexer #(.width(16), .enable("false")) multiplexer_1 (
    .in0({cpu_1_address_3, cpu_1_address_2, cpu_1_address}), .in1(ADDRESS_R), .out(multiplexer_1_out),
    .sel(ADDRESS_E));
  Multiplexer #(.width(8), .enable("false")) multiplexer_2 (
    .in0(cpu_1_data_out), .in1(DATA_R), .out(multiplexer_2_out), .sel(ADDRESS_E));
  or or_4 (CLCK, clock_1_out, TICK_TICK_BOOM_out);
  or or_5 (or_5_out, ADDRESS_E, cpu_1_mem_read);
  PowerSwitch powerswitch_1 (
    .CLCK_IN(CLCK), .SWITCH(POWER_ON), .RESET(RESET_C), .POWER_INDicator(P_O),
    .CLCK_OUT(powerswitch_1_clck_out));
  assign or_6_out = KEY_IN;  // OR_Gate or_6, 8 bits wide OR_Gate
  ROM #(.addrWidth(16)) rom_1 (.addr(ADDRESS_R), .data(DATA_R));  // open: sel
  RAM #(.addrWidth(16), .bus("separate")) ram_1 (
    .addr(multiplexer_1_out), .din(multiplexer_2_out), .data(ram_1_data), .str(or_5_out), .clk(CLCK));  // open: sel, ld, clr
  CPU cpu_1 (
    .DATA_IN(multiplexer_3_out), .CLCK(powerswitch_1_clck_out), .in_3(RESET),
    .SOFT_INTERRUPT(cpu_1_soft_interrupt), .MEM_READ(cpu_1_mem_read), .DATA_OUT(cpu_1_data_out),
    .Address({cpu_1_address_3, cpu_1_address_2, cpu_1_address}));
  Multiplexer #(.width(8), .enable("false")) multiplexer_3 (
    .in0(ram_1_data), .in1(or_6_out), .out(multiplexer_3_out), .sel(cpu_1_soft_interrupt));
  // Probe on multiplexer_3_out
  Demultiplexer #(.select(4), .width(8), .enable("false")) demultiplexer_1 (
    .out0(demultiplexer_1_out0), .out2(demultiplexer_1_out2), .in(cpu_1_data_out), .sel(cpu_1_address_2));  // open: out1, out3, out4, out5, out6, out7, out8, out9, out10, out11, out12, out13, out14, out15
  Decoder #(.select(4), .enable("false")) decoder_1 (
    .out0(decoder_1_out0), .out1(decoder_1_out1), .out2(decoder_1_out2), .sel(cpu_1_address_2));  // open: out3, out4, out5, out6, out7, out8, out9, out10, out11, out12, out13, out14, out15
  TTYControl ttycontrol_1 (
    .Data(demultiplexer_1_out0), .Selected(decoder_1_out0), .Function(cpu_1_address),
    .Interrupt(cpu_1_soft_interrupt), .in_5(CLCK), .Character(CHAR), .Write(CHAR_E), .CLR_TTY(CLR_SCREEN));
  KeyboardControl keyboardcontrol_1 (
    .Selected(decoder_1_out1), .Function(cpu_1_address), .Interrupt(cpu_1_soft_interrupt), .Buffer(CHAR_AV),
    .Key(CHAR_IN), .RESET(RESET), .Character(KEY_IN));
  GPUControl gpucontrol_1 (
    .Data(demultiplexer_1_out2), .Selected(decoder_1_out2), .Function(cpu_1_address),
    .Interrupt(cpu_1_soft_interrupt), .Coords(Coords), .Write(Trigger), .Pixel_value(P_V),
    .CLR_SCREEN(CLR_SCREEN_MEM), .CLCK(CLCK), .CLR(RESET));

  // Notes on the sheet:
  //   contents of rom_1 (hex, n*v repeats v):
  //   4b 0 4a 0 20 4a 0 5 4d 5 42 0 1 c1 e 10 4b 10 4a 0 28 1e 0 0 c2 5 2b 4b 0 4a 0 c 48 0 66 4b 0 4a 0 8
  //   41 a 1e 0 0 4d 1 42 1d 20 0 94 42 ff 20 0 96 20 0 95 c1 14 0 42 1e c1 d 12 10 0 93 10 0 97 41 3 1e 2
  //   1 41 80 42 a0 1e 2 3 c1 5 1b c1 e 12 4b 10 4a 0 9a 4b 0 4a 0 53 50 4f 4e 47 a 44 65 73 69 67 6e 65
  //   64 20 61 6e 64 20 50 72 6f 67 72 61 6d 6d 65 64 20 62 79 20 44 61 6e 69 65 6c 20 42 65 72 72 79 0 10
  //   10 ff ff 3 0 0 e1 1 0 4b 10 42 61 c1 e 12 4a 1 78 42 64 c1 e 12 4a 1 54 1 0 93 2 0 95 c1 6 12 1e 2 0
  //   2 0 94 1 0 96 c2 6 21 2e 2 4 1 0 93 1e 2 0 2 0 94 41 80 c2 5 12 2e 2 4 c2 6 21 4b 10 41 1e c2 e 21
  //   4a 1 c1 41 4 c2 e 21 4a 1 a1 41 1f 2 0 94 c2 e 21 4b 10 4a 2 14 1 0 96 2 0 94 c2 5 21 20 0 94 4b 10
  //   41 1f 2 0 93 c2 e 21 4a 1 b1 41 0 c2 e 21 4a 1 b1 1 0 95 2 0 93 c2 5 21 20 0 93 41 1f 1e 2 1 2 0 97
  //   41 80 c2 5 12 41 1 27 41 3 c7 5 17 2e 2 3 c2 5 2b c2 e 72 4b 10 4a 1 4f 4b 0 4a 1 3c 4b 0 4a 0 9a 1
  //   0 97 c1 5 1b 10 0 97 c1 6 1b 1e 2 0 41 1f 1e 2 4 42 82 1 0 97 c1 5 12 1e 2 3 4b 0 4a 0 af 1 0 97 c1
  //   6 1b 10 0 97 1 0 97 42 3 c1 5 12 1e 2 0 41 1f 1e 2 4 42 80 1 0 97 c1 5 12 1e 2 3 4b 0 4a 0 af 1 0 96
  //   42 ff c1 b 12 10 0 96 4b 0 4a 0 fa 1 0 95 42 ff c1 b 12 10 0 95 4b 0 4a 1 1b 1 0 93 2 0 97 c1 e 12
  //   4b 10 4a 1 a1 4b 20 4a 1 d9 4b 0 4a 0 fa 41 2 c2 5 12 1 0 93 c1 e 12 4b 20 4a 0 fa 1 0 99 c1 5 1b 10
  //   0 99 42 49 2e 0 0 4b 0 4a 1 a1 a 59 6f 75 20 73 75 63 6b 20 61 74 20 74 68 69 73 20 67 61 6d 65 2e 0
  //   4d 5 48 1 fc 42 0 1 c1 e 10 4b 10 4a 0 5 1e 0 0 c2 5 2b 4b 0 4a 2 1b ff a 55 73 65 20 57 41 53 44 20
  //   74 6f 20 6d 6f 76 65 20 74 68 65 20 63 75 72 73 6f 72 2e a 50 72 65 73 73 20 3c 53 70 61 63 65 3e 20
  //   74 6f 20 6d 61 72 6b 20 74 68 65 20 73 70 6f 74 2e a 50 72 65 73 73 20 3c 52 3e 20 74 6f 20 72 61 6e
  //   64 6f 6d 69 7a 65 2e a 50 72 65 73 73 20 3c 45 6e 74 65 72 3e 20 74 6f 20 73 74 61 72 74 2e a 50 72
  //   65 73 73 20 3c 51 3e 20 74 6f 20 71 75 69 74 2e 0 10 10 0 0 0 4d 5 48 2 30 42 0 1 c1 e 10 4b 10 4a 2
  //   d1 1e 0 0 c2 5 2b 4b 0 4a 2 bd 4d 1 41 10 10 2 b1 10 2 b2 1 2 b1 2 2 b2 1e 2 0 2e 2 4 e1 1 0 42 77
  //   c2 e 12 48 2 b2 42 ff 4b 10 4a 3 c6 42 61 c2 e 12 48 2 b1 42 ff 4a 3 c6 42 73 c2 e 12 48 2 b2 42 1
  //   4a 3 c6 42 64 c2 e 12 48 2 b1 42 1 4a 3 c6 42 20 42 72 42 a 1 2 b1 1e 2 0 41 80 2 2 b2 c2 5 12 2e 2
  //   4 4b 0 4a 2 db 42 0 47 0 4d 4 1 2 2f c1 13 17 c1 2 1b 45 80 c1 b 15 46 8 0 25 c5 b 56 c5 5 75 4d 1
  //   50 2 b3 46 20 0 5 2 b3 c5 c 56 10 2 b5 1 2 b4 c5 5 15 5e 2 0 46 20 0 5 2 b3 c5 d 56 1 2 b5 c5 5 15
  //   5e 2 4 c7 5 7b 41 8 c7 e 17 4b 10 4a 3 98 4b 0 4a 3 40 c2 5 2b 41 20 c2 e 12 4b 10 4a 3 aa 4b 0 4a 3
  //   c1 4d 1 5 2 b4 41 8 c5 5 51 50 2 b4 41 20 c5 e 15 4b 10 4a 3 37 4b 0 4a 3 3e 4d 3 1 c1 5 12 10 4d 1
  //   4b 0 4a 3 26 37 38 39 34 35 36 31 32 33 58 4d 4 42 0 41 58 10 3 dd 4b 0 4a 4 10 42 0 1 3 dd e2 1 0
  //   c2 e 20 4b 10 4a 3 ec 47 31 c2 6 27 10 3 d4 41 4f 42 0 10 3 dd 4b 0 4a 4 10 1e 0 1 42 0 1 3 d4 1e 0
  //   0 c2 5 2b 47 3 c7 d 27 4b 2 4a 4 2d 4b 0 4a 4 32 41 a 1e 0 0 47 9 c2 e 27 4b 10 4a 3 ec 4b 0 4a 4 15
endmodule

module CPU (
  input  [7:0] DATA_IN,
  input  CLCK,
  input  in_3,
  output [7:0] DATA_OUT,
  output SOFT_INTERRUPT,
  output MEM_READ,
  output [15:0] Address
);

  wire ADDR_plus_plus, ALU_CMD, and_1_out, and_3_out, decoder_1_out1, decoder_1_out2, decoder_1_out3,
       decoder_1_out4, decoder_1_out5, decoder_1_out6, decoder_1_out7, decoder_1_out8, decoder_1_out9,
       decoder_1_out10, decoder_1_out11, decoder_1_out12, decoder_1_out13, decoder_1_out14, FLAG_SAVE,
       INT_IN, JMP_CMD, JMP_CND, MOV, nand_1_out, or_2_out, PC0_carry, PC_plus_plus;
  wire [3:0] Address_Select, DEST, Opcode_q, Opcode_q_2, SRC;
  wire [7:0] A_q, Address_Mode_q, ALU1, ALU2, alu_1_out_6, alu_1_outflags, and_4_out, ARG_0_q, ARG_1_q, B_q,
       CMP_Test_q, Flags_q, IND_0_q, IND_1_q, PC0_q, PC1_q, SP0_q, SP1_q, xor_1_out;
  wire [15:0] adder_1_out, adder_2_out, adder_3_out, adder_4_out, multiplexer_4_out;
  wire [15:8] pull_resistor_1_node, pull_resistor_4_node;

  and and_1 (and_1_out, MOV, INT_IN);
  and and_2 (FLAG_SAVE, MOV, ALU_CMD);
  or or_1 (SOFT_INTERRUPT, and_1_out, decoder_1_out14);
  Decoder #(.select(4), .disabled(0)) decoder_1 (
    .out0(MEM_READ), .out1(decoder_1_out1), .out2(decoder_1_out2), .out3(decoder_1_out3),
    .out4(decoder_1_out4), .out5(decoder_1_out5), .out6(decoder_1_out6), .out7(decoder_1_out7),
    .out8(decoder_1_out8), .out9(decoder_1_out9), .out10(decoder_1_out10), .out11(decoder_1_out11),
    .out12(decoder_1_out12), .out13(decoder_1_out13), .out14(decoder_1_out14), .sel(DEST), .en(or_2_out));  // open: out15
  or or_2 (or_2_out, nand_1_out, ~MOV);  // OR_Gate
  nand nand_1 (nand_1_out, JMP_CMD, MOV, ~JMP_CND);  // NAND_Gate
  Register A (.D(DATA_OUT), .en(decoder_1_out1), .Q(A_q), .clk(CLCK), .clr(in_3));
  Register B (.D(DATA_OUT), .en(decoder_1_out2), .Q(B_q), .clk(CLCK), .clr(in_3));
  Register ARG_0 (.D(DATA_OUT), .en(decoder_1_out3), .Q(ARG_0_q), .clk(CLCK), .clr(in_3));
  Register ARG_1 (.D(DATA_OUT), .en(decoder_1_out4), .Q(ARG_1_q), .clk(CLCK), .clr(in_3));
  Register SP0 (.D(DATA_OUT), .en(decoder_1_out5), .Q(SP0_q), .clk(CLCK), .clr(in_3));
  Register SP1 (.D(DATA_OUT), .en(decoder_1_out6), .Q(SP1_q), .clk(CLCK), .clr(in_3));
  Register IND_0 (.D(DATA_OUT), .en(decoder_1_out7), .Q(IND_0_q), .clk(CLCK), .clr(in_3));
  Register IND_1 (.D(DATA_OUT), .en(decoder_1_out8), .Q(IND_1_q), .clk(CLCK), .clr(in_3));
  Counter PC0 (
    .load(decoder_1_out9), .D(DATA_OUT), .count(PC_plus_plus), .Q(PC0_q), .carry(PC0_carry), .clk(CLCK),
    .clr(in_3));
  Counter PC1 (
    .load(decoder_1_out10), .D(DATA_OUT), .count(and_3_out), .Q(PC1_q), .clk(CLCK), .clr(in_3));  // open: carry
  and and_3 (and_3_out, PC_plus_plus, PC0_carry);
  Register CMP_Test (.D(DATA_OUT), .en(decoder_1_out11), .Q(CMP_Test_q), .clk(CLCK), .clr(in_3));
  Register Flags (.D(alu_1_outflags), .en(FLAG_SAVE), .Q(Flags_q), .clk(CLCK), .clr(in_3));
  ALU alu_1 (.InFlags(Flags_q), ._1(ALU1), ._0(ALU2), .OutFlags(alu_1_outflags), .out_6(alu_1_out_6), .in_4(ARG_1_q));
  Register Opcode (.D(DATA_OUT), .en(decoder_1_out12), .Q({Opcode_q_2, Opcode_q}), .clk(CLCK), .clr(in_3));
  Register Address_Mode (.D(DATA_OUT), .en(decoder_1_out13), .Q(Address_Mode_q), .clk(CLCK), .clr(in_3));
  Control control_1 (
    .CLCK(CLCK), .Opcode({Opcode_q_2, Opcode_q}), .Address_Mode(Address_Mode_q), .PC_plus_plus(PC_plus_plus),
    .MOV(MOV), .CLR(in_3), .ADDR___1(ADDR_plus_plus), .SRC(SRC), .DEST(DEST), .Address_Pull(Address_Select));
  Comparator #(.width(4)) comparator_1 (.a(Opcode_q), .b(4'b1010), .eq(JMP_CMD));  // open: gt, lt
  Comparator #(.width(4)) comparator_2 (.a(Opcode_q_2), .b(4'b1100), .eq(ALU_CMD));  // open: gt, lt
  Comparator #(.width(4)) comparator_3 (.a(Opcode_q_2), .b(4'b1110), .eq(INT_IN));  // open: gt, lt
  Pull_Resistor pull_resistor_1 (.node({pull_resistor_1_node, B_q}));
  Adder #(.width(16)) adder_1 (
    .a({IND_1_q, IND_0_q}), .b({pull_resistor_1_node, B_q}), .out(adder_1_out));  // open: cin, cout
  Adder #(.width(16)) adder_2 (
    .a({SP1_q, SP0_q}), .b({pull_resistor_4_node, ARG_1_q}), .out(adder_2_out));  // open: cin, cout
  assign xor_1_out = CMP_Test_q ^ and_4_out;  // XOR_Gate xor_1, 8 bits wide
  assign and_4_out = CMP_Test_q & Flags_q;  // AND_Gate and_4, 8 bits wide
  Multiplexer #(.select(4), .width(8), .enable("false")) multiplexer_1 (
    .in0(DATA_IN), .in1(A_q), .in2(B_q), .in3(ARG_0_q), .in4(ARG_1_q), .in5(SP0_q), .in6(SP1_q),
    .in7(IND_0_q), .in8(IND_1_q), .in9(PC0_q), .in10(PC1_q), .in12(alu_1_out_6), .in14(DATA_IN),
    .out(DATA_OUT), .sel(SRC));  // open: in11, in13, in15
  // Probe on SRC
  Pull_Resistor pull_resistor_2 (.node(ALU1));
  Multiplexer #(.select(4), .width(8), .enable("false")) multiplexer_2 (
    .in0({8{1'b0}}), .in1(A_q), .in2(B_q), .in3(ARG_0_q), .in4(ARG_1_q), .in5(SP0_q), .in6(SP1_q),
    .in7(IND_0_q), .in8(IND_1_q), .in9(PC0_q), .in10(PC1_q), .in11(8'h1), .in12(8'h2), .out(ALU1),
    .sel(ARG_0_q[3:0]));  // open: in13, in14, in15
  Pull_Resistor pull_resistor_3 (.node(ALU2));
  Multiplexer #(.select(4), .width(8), .enable("false")) multiplexer_3 (
    .in0({8{1'b0}}), .in1(A_q), .in2(B_q), .in3(ARG_0_q), .in4(ARG_1_q), .in5(SP0_q), .in6(SP1_q),
    .in7(IND_0_q), .in8(IND_1_q), .in9(PC0_q), .in10(PC1_q), .in11(8'h1), .in12(8'h2), .out(ALU2),
    .sel(ARG_0_q[7:4]));  // open: in13, in14, in15
  Pull_Resistor pull_resistor_4 (.node({pull_resistor_4_node, ARG_1_q}));
  Adder #(.width(16)) adder_3 (
    .a({ARG_1_q, ARG_0_q}), .b({pull_resistor_1_node, B_q}), .out(adder_3_out));  // open: cin, cout
  Comparator comparator_4 (.a(xor_1_out), .b({8{1'b0}}), .eq(JMP_CND));  // open: gt, lt
  // Probe on DATA_OUT
  // Probe on Address_Select
  Multiplexer #(.select(4), .width(16), .enable("false")) multiplexer_4 (
    .in0({PC1_q, PC0_q}), .in1({ARG_1_q, ARG_0_q}), .in2(adder_2_out), .in3({IND_1_q, IND_0_q}),
    .in4(adder_3_out), .in5(adder_1_out), .out(multiplexer_4_out), .sel(Address_Select));  // open: in6, in7, in8, in9, in10, in11, in12, in13, in14, in15
  Adder #(.width(16)) adder_4 (.a(multiplexer_4_out), .b(16'h1), .out(adder_4_out));  // open: cin, cout
  Multiplexer #(.width(16), .enable("false")) multiplexer_5 (
    .in0(multiplexer_4_out), .in1(adder_4_out), .out(Address), .sel(ADDR_plus_plus));
  // Probe on Address

  // Other names for the same wires on the sheet: DATA[7:0] = DATA_OUT

  // Notes on the sheet:
  //   0 - PC
  //   1 - Direct
  //   2 - Stack
  //   3 - Indirect
  //   4 - Direct + B
  //   5 - Indirect + B
endmodule

module Control (
  input  CLCK,
  input  [7:0] Opcode,
  input  [7:0] Address_Mode,
  input  CLR,
  output PC_plus_plus,
  output MOV,
  output [3:0] SRC,
  output [3:0] DEST,
  output [3:0] Address_Pull,
  output ADDR___1
);

  wire and_1_out, comparator_1_eq, comparator_2_eq, comparator_3_eq, comparator_4_eq, decoder_1_out0,
       decoder_1_out1, decoder_1_out2, decoder_1_out3, decoder_1_out4, decoder_1_out5, Load, not_1_out,
       or_1_out, or_3_out, or_4_out, write_table_1_address___1, write_table_1_in_1, write_table_1_out_1,
       write_table_1_write_num_1;
  wire [1:0] Num_Args, priority_encoder_1_out;
  wire [2:0] counter_1_q;
  wire [3:0] adder_1_out, bit_extender_1_out, bit_extender_2_out, multiplexer_1_out, multiplexer_2_out,
       multiplexer_3_out, multiplexer_4_out, subtractor_1_out, subtractor_2_out;

  Counter #(.width(3), .max('h7), .trigger("falling")) counter_1 (
    .load(Load), .D(3'b011), .count(not_1_out), .Q(counter_1_q), .clk(CLCK), .clr(or_1_out));  // open: carry
  not not_1 (not_1_out, Load);
  or or_1 (or_1_out, comparator_1_eq, or_3_out);
  Comparator comparator_1 (.a({8{1'b0}}), .b(Opcode), .eq(comparator_1_eq));  // open: gt, lt
  Arg_Table arg_table_1 (.in_1(Opcode), .in_2(Address_Mode[3:0]), .ARG_Number(Num_Args));
  Comparator #(.width(4)) comparator_2 (.a(Opcode[3:0]), .b(4'b1110), .eq(comparator_2_eq));  // open: gt, lt
  Comparator #(.width(4)) comparator_3 (.a(Opcode[7:4]), .b(4'b1110), .eq(comparator_3_eq));  // open: gt, lt
  or or_2 (PC_plus_plus, decoder_1_out0, decoder_1_out1, decoder_1_out2);
  Decoder #(.select(3), .enable("false")) decoder_1 (
    .out0(decoder_1_out0), .out1(decoder_1_out1), .out2(decoder_1_out2), .out3(decoder_1_out3),
    .out4(decoder_1_out4), .out5(decoder_1_out5), .sel(counter_1_q));  // open: out6, out7
  or or_3 (or_3_out, decoder_1_out5, and_1_out, CLR);
  Write_Table write_table_1 (
    .Opcode(Opcode), .Out_1(write_table_1_out_1), .Address___1(write_table_1_address___1),
    .WRITE_NUM_1(write_table_1_write_num_1), .In_1(write_table_1_in_1));
  or or_4 (or_4_out, comparator_2_eq, comparator_3_eq);
  or or_5 (MOV, decoder_1_out3, decoder_1_out4);
  and and_1 (and_1_out, decoder_1_out4, ~write_table_1_write_num_1);  // AND_Gate
  Comparator #(.width(4), .mode("unsigned")) comparator_4 (
    .a(Opcode[7:4]), .b(4'b0011), .eq(comparator_4_eq));  // open: gt, lt
  // Probe on Num_Args
  Priority_Encoder #(.select(2)) priority_encoder_1 (
    .in0(decoder_1_out0), .in1(decoder_1_out1), .in2(decoder_1_out2), .out(priority_encoder_1_out));  // open: in3, gs, en_out, en_in
  Pull_Resistor #(.pull(1)) pull_resistor_1 (.node(priority_encoder_1_out));
  and and_2 (ADDR___1, write_table_1_address___1, decoder_1_out4);
  Comparator #(.width(2), .mode("unsigned")) comparator_5 (
    .a(Num_Args), .b(priority_encoder_1_out), .eq(Load));  // open: gt, lt
  assign bit_extender_1_out = {{3{1'b0}}, write_table_1_in_1};  // Bit_Extender bit_extender_1
  Subtractor #(.width(4)) subtractor_1 (
    .a(Opcode[3:0]), .b(bit_extender_2_out), .out(subtractor_1_out));  // open: bin, bout
  assign bit_extender_2_out = {{3{1'b0}}, write_table_1_out_1};  // Bit_Extender bit_extender_2
  Adder #(.width(4)) adder_1 (.a(Opcode[7:4]), .b(bit_extender_1_out), .out(adder_1_out));  // open: cin, cout
  Multiplexer #(.width(4), .enable("false")) multiplexer_1 (
    .in0(Opcode[7:4]), .in1(adder_1_out), .out(multiplexer_1_out), .sel(comparator_4_eq));
  Subtractor #(.width(4)) subtractor_2 (
    .a(Opcode[7:4]), .b(bit_extender_1_out), .out(subtractor_2_out));  // open: bin, bout
  Multiplexer #(.width(4), .enable("false")) multiplexer_2 (
    .in0(subtractor_2_out), .in1(Opcode[7:4]), .out(multiplexer_2_out), .sel(comparator_4_eq));
  Multiplexer #(.width(4), .enable("false")) multiplexer_3 (
    .in0(Address_Mode[3:0]), .in1(4'b0001), .out(multiplexer_3_out), .sel(or_4_out));
  Multiplexer #(.width(4), .enable("false")) multiplexer_4 (
    .in0(Address_Mode[3:0]), .in1(4'b0001), .out(multiplexer_4_out), .sel(or_4_out));
  Multiplexer #(.select(3), .width(4), .enable("false")) multiplexer_5 (
    .in0(4'b0000), .in1(4'b0000), .in2(4'b0000), .in3(multiplexer_1_out), .in4(multiplexer_2_out), .out(SRC),
    .sel(counter_1_q));  // open: in5, in6, in7
  Multiplexer #(.select(3), .width(4), .enable("false")) multiplexer_6 (
    .in0(4'b1100), .in1(4'b0100), .in2(4'b0011), .in3(Opcode[3:0]), .in4(subtractor_1_out), .out(DEST),
    .sel(counter_1_q));  // open: in5, in6, in7
  Multiplexer #(.select(3), .width(4), .enable("false")) multiplexer_7 (
    .in0(4'b0000), .in1(4'b0000), .in2(4'b0000), .in3(multiplexer_3_out), .in4(multiplexer_4_out),
    .out(Address_Pull), .sel(counter_1_q));  // open: in5, in6, in7
endmodule

module Arg_Table (
  input  [7:0] in_1,
  input  [3:0] in_2,
  output [1:0] ARG_Number
);

  wire and_1_out, decoder_1_out0, decoder_1_out3, decoder_1_out4, decoder_1_out6, decoder_1_out8,
       decoder_1_out10, decoder_1_out14, decoder_2_out0, decoder_2_out3, decoder_2_out4, decoder_2_out12,
       decoder_2_out14, decoder_3_out1, decoder_3_out2, decoder_3_out4, or_1_out, or_2_out, or_3_out,
       or_4_out, or_5_out, or_6_out, or_7_out;

  Decoder #(.select(4), .enable("false")) decoder_1 (
    .out0(decoder_1_out0), .out3(decoder_1_out3), .out4(decoder_1_out4), .out6(decoder_1_out6),
    .out8(decoder_1_out8), .out10(decoder_1_out10), .out14(decoder_1_out14), .sel(in_1[3:0]));  // open: out1, out2, out5, out7, out9, out11, out12, out13, out15
  Decoder #(.select(4), .enable("false")) decoder_2 (
    .out0(decoder_2_out0), .out3(decoder_2_out3), .out4(decoder_2_out4), .out12(decoder_2_out12),
    .out14(decoder_2_out14), .sel(in_1[7:4]));  // open: out1, out2, out5, out6, out7, out8, out9, out10, out11, out13, out15
  or or_1 (or_1_out, decoder_1_out6, decoder_1_out8, decoder_1_out10);
  or or_2 (or_2_out, decoder_1_out0, decoder_2_out0);
  Decoder #(.select(4)) decoder_3 (
    .out1(decoder_3_out1), .out2(decoder_3_out2), .out4(decoder_3_out4), .sel(in_2), .en(or_2_out));  // open: out0, out3, out5, out6, out7, out8, out9, out10, out11, out12, out13, out14, out15
  or or_3 (or_3_out, decoder_2_out4, decoder_3_out2, or_4_out);
  or or_4 (or_4_out, decoder_1_out3, decoder_1_out4);
  and and_1 (and_1_out, decoder_2_out4, or_1_out);
  or or_5 (or_5_out, decoder_2_out14, decoder_1_out14);
  Priority_Encoder #(.select(2)) priority_encoder_1 (
    .in1(or_3_out), .in2(or_6_out), .out(ARG_Number));  // open: in0, in3, gs, en_out, en_in
  Pull_Resistor pull_resistor_1 (.node(ARG_Number));
  or or_6 (or_6_out, decoder_2_out3, decoder_3_out4, or_7_out);
  or or_7 (or_7_out, decoder_3_out1, and_1_out, or_5_out, decoder_2_out12);
endmodule

module Write_Table (
  input  [7:0] Opcode,
  output Out_1,
  output Address___1,
  output WRITE_NUM_1,
  output In_1
);

  wire and_1_out, and_2_out, and_3_out, and_4_out, decoder_1_out0, decoder_1_out3, decoder_1_out4,
       decoder_1_out6, decoder_1_out8, decoder_1_out10, decoder_2_out0, decoder_2_out2, decoder_2_out4,
       decoder_2_out6, decoder_2_out8, decoder_2_out10, or_1_out, or_2_out;

  Decoder #(.select(4), .enable("false")) decoder_1 (
    .out0(decoder_1_out0), .out3(decoder_1_out3), .out4(decoder_1_out4), .out6(decoder_1_out6),
    .out8(decoder_1_out8), .out10(decoder_1_out10), .sel(Opcode[7:4]));  // open: out1, out2, out5, out7, out9, out11, out12, out13, out14, out15
  Decoder #(.select(4), .enable("false")) decoder_2 (
    .out0(decoder_2_out0), .out2(decoder_2_out2), .out4(decoder_2_out4), .out6(decoder_2_out6),
    .out8(decoder_2_out8), .out10(decoder_2_out10), .sel(Opcode[3:0]));  // open: out1, out3, out5, out7, out9, out11, out12, out13, out14, out15
  or or_1 (or_1_out, decoder_1_out3, decoder_1_out4, decoder_1_out6, decoder_1_out8, decoder_1_out10);
  and and_1 (and_1_out, decoder_1_out3, decoder_2_out2);
  or or_2 (or_2_out, decoder_2_out4, decoder_2_out6, decoder_2_out8, decoder_2_out10);
  and and_2 (and_2_out, decoder_1_out0, or_2_out);
  and and_3 (and_3_out, or_1_out, or_2_out);
  and and_4 (and_4_out, or_1_out, decoder_2_out0);
  or or_3 (Out_1, and_2_out, and_1_out, and_3_out);
  or or_4 (Address___1, and_2_out, and_4_out);
  or or_5 (In_1, and_3_out, and_1_out, and_4_out);
  or or_6 (WRITE_NUM_1, Out_1, Address___1, In_1);
endmodule

module ALU (
  input  [7:0] InFlags,
  input  [7:0] _1,
  input  [7:0] _0,
  input  [7:0] in_4,
  output [7:0] OutFlags,
  output [7:0] out_6
);

  wire adder_1_cout, adder_2_cout, adder_3_cout, bitselector_1_out, comparator_3_eq, not_3_out,
       subtractor_1_bout, subtractor_2_bout, subtractor_3_bout;
  wire [7:0] adder_1_out, adder_2_out, and_1_out, divider_1_out, divider_1_rem, multiplier_1_out,
       negator_1_out, negator_2_out, not_1_out, not_2_out, or_1_out, random_1_out, shifter_1_out,
       shifter_2_out, shifter_3_out, shifter_4_out, shifter_5_out, subtractor_1_out, subtractor_2_out,
       subtractor_3_out, undriven, undriven_2, xor_1_out;

  BitSelector bitselector_1 (.in(InFlags), .out(bitselector_1_out), .sel(3'b000));
  assign not_1_out = ~_0;  // NOT_Gate not_1, 8 bits wide
  assign not_2_out = ~_1;  // NOT_Gate not_2, 8 bits wide
  assign and_1_out = _0 & _1;  // AND_Gate and_1, 8 bits wide
  assign or_1_out = _0 | _1;  // OR_Gate or_1, 8 bits wide
  assign xor_1_out = _0 ^ _1;  // XOR_Gate xor_1, 8 bits wide
  Adder adder_1 (.a(_0), .b(_1), .out(adder_1_out), .cout(adder_1_cout));  // open: cin
  Subtractor subtractor_1 (.a(_0), .b(_1), .out(subtractor_1_out), .bout(subtractor_1_bout));  // open: bin
  Adder adder_2 (.a(_0), .b(_1), .out(adder_2_out), .cin(bitselector_1_out), .cout(adder_2_cout));
  Subtractor subtractor_2 (.a(_0), .b(_1), .out(subtractor_2_out), .bin(bitselector_1_out), .bout(subtractor_2_bout));
  Negator negator_1 (.in(_0), .out(negator_1_out));
  Negator negator_2 (.in(_1), .out(negator_2_out));
  Multiplier multiplier_1 (.a(_0), .b(_1), .out(multiplier_1_out));  // open: cin, cout
  Divider divider_1 (.a(_0), .b(_1), .out(divider_1_out), .rem(divider_1_rem));  // open: upper
  Comparator comparator_1 (.a(subtractor_1_out), .b({8{1'b0}}), .gt(OutFlags[5]), .eq(OutFlags[4]));  // open: lt
  Comparator #(.mode("unsigned")) comparator_2 (.a(undriven_2), .b(undriven), .gt(OutFlags[6]));  // open: eq, lt
  Shifter shifter_1 (.in(_0), .\dist (_1[2:0]), .out(shifter_1_out));
  Shifter #(.shift("lr")) shifter_2 (.in(_0), .\dist (_1[2:0]), .out(shifter_2_out));
  Shifter #(.shift("ar")) shifter_3 (.in(_0), .\dist (_1[2:0]), .out(shifter_3_out));
  Shifter #(.shift("rl")) shifter_4 (.in(_0), .\dist (_1[2:0]), .out(shifter_4_out));
  Shifter #(.shift("rr")) shifter_5 (.in(_0), .\dist (_1[2:0]), .out(shifter_5_out));
  Random random_1 (.clk(comparator_3_eq), .out(random_1_out));  // open: next, clr
  Adder #(.width(7)) adder_3 (.a(_0[6:0]), .b(_1[6:0]), .cout(adder_3_cout));  // open: out, cin
  Multiplexer #(.select(2), .disabled(0)) multiplexer_1 (
    .in0(adder_1_cout), .in1(subtractor_1_bout), .in2(adder_2_cout), .in3(subtractor_2_bout),
    .out(OutFlags[0]), .sel(subtractor_3_out[1:0]), .en(not_3_out));
  xor xor_2 (OutFlags[2], OutFlags[0], adder_3_cout);
  Pull_Resistor pull_resistor_1 (.node(OutFlags));
  Comparator #(.width(5)) comparator_3 (.a(in_4[4:0]), .b(5'b10100), .eq(comparator_3_eq));  // open: gt, lt
  Multiplexer #(.select(5), .width(8), .enable("false")) multiplexer_2 (
    .in0(not_1_out), .in1(not_2_out), .in2(and_1_out), .in3(or_1_out), .in4(xor_1_out), .in5(adder_1_out),
    .in6(subtractor_1_out), .in7(adder_2_out), .in8(subtractor_2_out), .in9(negator_1_out),
    .in10(negator_2_out), .in11(multiplier_1_out), .in12(divider_1_out), .in13(divider_1_rem),
    .in15(shifter_1_out), .in16(shifter_2_out), .in17(shifter_3_out), .in18(shifter_4_out),
    .in19(shifter_5_out), .in20(random_1_out), .out(out_6), .sel(in_4[4:0]));  // open: in14, in21, in22, in23, in24, in25, in26, in27, in28, in29, in30, in31
  Comparator comparator_4 (.a({8{1'b0}}), .b(out_6), .gt(OutFlags[3]), .eq(OutFlags[1]));  // open: lt
  Subtractor subtractor_3 (.a(in_4), .b(8'h5), .out(subtractor_3_out), .bout(subtractor_3_bout));  // open: bin
  not not_3 (not_3_out, subtractor_3_bout);

  // Notes on the sheet:
  //   gGENVZC
endmodule

module TTYControl (
  input  [7:0] Data,
  input  Selected,
  input  [7:0] Function,
  input  Interrupt,
  input  in_5,
  output [6:0] Character,
  output Write,
  output CLR_TTY
);

  wire and_1_out, decoder_1_out1;
  wire [7:7] demultiplexer_1_out0;

  and and_1 (and_1_out, Selected, Interrupt);
  Demultiplexer #(.select(4), .width(8), .disabled(0)) demultiplexer_1 (
    .out0({demultiplexer_1_out0[7], Character}), .in(Data), .sel(Function[3:0]), .en(Selected));  // open: out1, out2, out3, out4, out5, out6, out7, out8, out9, out10, out11, out12, out13, out14, out15
  Decoder #(.select(4), .disabled(0)) decoder_1 (
    .out0(Write), .out1(decoder_1_out1), .sel(Function[3:0]), .en(and_1_out));  // open: out2, out3, out4, out5, out6, out7, out8, out9, out10, out11, out12, out13, out14, out15
  Pull_Resistor pull_resistor_1 (.node(CLR_TTY));
  assign CLR_TTY = in_5 ? decoder_1_out1 : 1'bz;  // Controlled_Buffer controlled_buffer_1
endmodule

module KeyboardControl (
  input  Selected,
  input  [7:0] Function,
  input  Interrupt,
  input  Buffer,
  input  [6:0] Key,
  input  RESET,
  output [7:0] Character
);

  wire and_1_out, decoder_1_out0, or_1_out;
  wire [3:0] counter_1_q, multiplexer_1_out;
  wire [6:0] multiplexer_2_out, ram_1_data;

  and and_1 (and_1_out, Selected, Interrupt);
  Decoder #(.select(4), .disabled(0)) decoder_1 (
    .out0(decoder_1_out0), .sel(Function[3:0]), .en(and_1_out));  // open: out1, out2, out3, out4, out5, out6, out7, out8, out9, out10, out11, out12, out13, out14, out15
  or or_1 (or_1_out, decoder_1_out0, Buffer);
  Counter #(.width(4), .max('hf), .ongoal("stay")) counter_1 (
    .load(decoder_1_out0), .count(or_1_out), .Q(counter_1_q), .clk(or_1_out), .clr(RESET));  // open: D, carry
  Multiplexer #(.width(4), .enable("false")) multiplexer_1 (
    .in0(counter_1_q), .in1(4'b0000), .out(multiplexer_1_out), .sel(decoder_1_out0));
  RAM #(.addrWidth(4), .dataWidth(7), .bus("separate")) ram_1 (
    .addr(multiplexer_1_out), .din(Key), .data(ram_1_data), .clk(or_1_out), .clr(RESET));  // open: str, sel, ld
  assign Character = {{1{1'b0}}, multiplexer_2_out};  // Bit_Extender bit_extender_1
  Multiplexer #(.select(4), .width(7)) multiplexer_2 (
    .in0(ram_1_data), .out(multiplexer_2_out), .sel(Function[3:0]), .en(and_1_out));  // open: in1, in2, in3, in4, in5, in6, in7, in8, in9, in10, in11, in12, in13, in14, in15
endmodule

module Program_Loader (
  input  CLCK,
  input  WRITE,
  input  RESET,
  output [15:0] ADDRESS,
  output WRITING
);

  wire counter_1_carry, or_1_out, t_ff_1_qn;

  Counter #(.width(16), .max('hffff)) counter_1 (
    .count(WRITING), .Q(ADDRESS), .carry(counter_1_carry), .clk(CLCK), .clr(t_ff_1_qn));  // open: load, D
  T_Flip_Flop t_ff_1 (.clk(WRITE), .T(1'b1), .Q(WRITING), .Qn(t_ff_1_qn), .reset(or_1_out));  // open: preset, en
  or or_1 (or_1_out, RESET, counter_1_carry);
endmodule

module PowerSwitch (
  input  SWITCH,
  input  CLCK_IN,
  output POWER_INDicator,
  output CLCK_OUT,
  output RESET
);

  T_Flip_Flop t_ff_1 (.clk(SWITCH), .T(1'b1), .Q(POWER_INDicator));  // open: Qn, preset, reset, en
  and and_1 (CLCK_OUT, POWER_INDicator, CLCK_IN);

  assign RESET = SWITCH;
endmodule

module GPU (
  input  [4:0] SELECT_Y,
  input  CLR_WRITE,
  input  [4:0] SELECT_X,
  input  CLCK,
  input  CLR,
  output [31:0] out_6,
  output [31:0] out_7,
  output [31:0] out_8,
  output [31:0] out_9,
  output [31:0] out_10,
  output [31:0] out_11,
  output [31:0] out_12,
  output [31:0] out_13,
  output [31:0] out_14,
  output [31:0] out_15,
  output [31:0] out_16,
  output [31:0] out_17,
  output [31:0] out_18,
  output [31:0] out_19,
  output [31:0] out_20,
  output [31:0] out_21,
  output [31:0] out_22,
  output [31:0] out_23,
  output [31:0] out_24,
  output [31:0] out_25,
  output [31:0] out_26,
  output [31:0] out_27,
  output [31:0] out_28,
  output [31:0] out_29,
  output [31:0] out_30,
  output [31:0] out_31,
  output [31:0] out_32,
  output [31:0] out_33,
  output [31:0] out_34,
  output [31:0] out_35,
  output [31:0] out_36,
  output [31:0] out_37
);

  wire decoder_1_out0, decoder_1_out1, decoder_1_out2, decoder_1_out3, decoder_1_out4, decoder_1_out5,
       decoder_1_out6, decoder_1_out7, decoder_1_out8, decoder_1_out9, decoder_1_out10, decoder_1_out11,
       decoder_1_out12, decoder_1_out13, decoder_1_out14, decoder_1_out15, decoder_2_out0, decoder_2_out1,
       decoder_2_out2, decoder_2_out3, decoder_2_out4, decoder_2_out5, decoder_2_out6, decoder_2_out7,
       decoder_2_out8, decoder_2_out9, decoder_2_out10, decoder_2_out11, decoder_2_out12, decoder_2_out13,
       decoder_2_out14, decoder_2_out15, not_1_out;
  wire [31:0] multiplexer_1_out, P_D, shifter_1_out;

  not not_1 (not_1_out, SELECT_X[4]);
  Decoder #(.select(4), .disabled(0)) decoder_1 (
    .out0(decoder_1_out0), .out1(decoder_1_out1), .out2(decoder_1_out2), .out3(decoder_1_out3),
    .out4(decoder_1_out4), .out5(decoder_1_out5), .out6(decoder_1_out6), .out7(decoder_1_out7),
    .out8(decoder_1_out8), .out9(decoder_1_out9), .out10(decoder_1_out10), .out11(decoder_1_out11),
    .out12(decoder_1_out12), .out13(decoder_1_out13), .out14(decoder_1_out14), .out15(decoder_1_out15),
    .sel(SELECT_X[3:0]), .en(not_1_out));
  // Probe on P_D
  Register #(.width(32), .trigger("falling")) register_1 (
    .D(P_D), .en(decoder_1_out0), .Q(out_6), .clk(CLCK), .clr(CLR));
  Register #(.width(32), .trigger("falling")) register_2 (
    .D(P_D), .en(decoder_1_out1), .Q(out_7), .clk(CLCK), .clr(CLR));
  Register #(.width(32), .trigger("falling")) register_3 (
    .D(P_D), .en(decoder_1_out2), .Q(out_8), .clk(CLCK), .clr(CLR));
  Register #(.width(32), .trigger("falling")) register_4 (
    .D(P_D), .en(decoder_1_out3), .Q(out_9), .clk(CLCK), .clr(CLR));
  Register #(.width(32), .trigger("falling")) register_5 (
    .D(P_D), .en(decoder_1_out4), .Q(out_10), .clk(CLCK), .clr(CLR));
  Register #(.width(32), .trigger("falling")) register_6 (
    .D(P_D), .en(decoder_1_out5), .Q(out_11), .clk(CLCK), .clr(CLR));
  Register #(.width(32), .trigger("falling")) register_7 (
    .D(P_D), .en(decoder_1_out6), .Q(out_12), .clk(CLCK), .clr(CLR));
  Register #(.width(32), .trigger("falling")) register_8 (
    .D(P_D), .en(decoder_1_out7), .Q(out_13), .clk(CLCK), .clr(CLR));
  Register #(.width(32), .trigger("falling")) register_9 (
    .D(P_D), .en(decoder_1_out8), .Q(out_14), .clk(CLCK), .clr(CLR));
  Register #(.width(32), .trigger("falling")) register_10 (
    .D(P_D), .en(decoder_1_out9), .Q(out_15), .clk(CLCK), .clr(CLR));
  Register #(.width(32), .trigger("falling")) register_11 (
    .D(P_D), .en(decoder_1_out10), .Q(out_16), .clk(CLCK), .clr(CLR));
  Register #(.width(32), .trigger("falling")) register_12 (
    .D(P_D), .en(decoder_2_out0), .Q(out_22), .clk(CLCK), .clr(CLR));
  Decoder #(.select(4), .disabled(0)) decoder_2 (
    .out0(decoder_2_out0), .out1(decoder_2_out1), .out2(decoder_2_out2), .out3(decoder_2_out3),
    .out4(decoder_2_out4), .out5(decoder_2_out5), .out6(decoder_2_out6), .out7(decoder_2_out7),
    .out8(decoder_2_out8), .out9(decoder_2_out9), .out10(decoder_2_out10), .out11(decoder_2_out11),
    .out12(decoder_2_out12), .out13(decoder_2_out13), .out14(decoder_2_out14), .out15(decoder_2_out15),
    .sel(SELECT_X[3:0]), .en(SELECT_X[4]));
  Register #(.width(32), .trigger("falling")) register_13 (
    .D(P_D), .en(decoder_1_out11), .Q(out_17), .clk(CLCK), .clr(CLR));
  Register #(.width(32), .trigger("falling")) register_14 (
    .D(P_D), .en(decoder_1_out12), .Q(out_18), .clk(CLCK), .clr(CLR));
  Register #(.width(32), .trigger("falling")) register_15 (
    .D(P_D), .en(decoder_1_out13), .Q(out_19), .clk(CLCK), .clr(CLR));
  Register #(.width(32), .trigger("falling")) register_16 (
    .D(P_D), .en(decoder_2_out1), .Q(out_23), .clk(CLCK), .clr(CLR));
  Register #(.width(32), .trigger("falling")) register_17 (
    .D(P_D), .en(decoder_2_out2), .Q(out_24), .clk(CLCK), .clr(CLR));
  Register #(.width(32), .trigger("falling")) register_18 (
    .D(P_D), .en(decoder_2_out3), .Q(out_25), .clk(CLCK), .clr(CLR));
  Register #(.width(32), .trigger("falling")) register_19 (
    .D(P_D), .en(decoder_1_out14), .Q(out_20), .clk(CLCK), .clr(CLR));
  Register #(.width(32), .trigger("falling")) register_20 (
    .D(P_D), .en(decoder_1_out15), .Q(out_21), .clk(CLCK), .clr(CLR));
  Register #(.width(32), .trigger("falling")) register_21 (
    .D(P_D), .en(decoder_2_out4), .Q(out_26), .clk(CLCK), .clr(CLR));
  Register #(.width(32), .trigger("falling")) register_22 (
    .D(P_D), .en(decoder_2_out5), .Q(out_27), .clk(CLCK), .clr(CLR));
  Register #(.width(32), .trigger("falling")) register_23 (
    .D(P_D), .en(decoder_2_out6), .Q(out_28), .clk(CLCK), .clr(CLR));
  Register #(.width(32), .trigger("falling")) register_24 (
    .D(P_D), .en(decoder_2_out7), .Q(out_29), .clk(CLCK), .clr(CLR));
  Register #(.width(32), .trigger("falling")) register_25 (
    .D(P_D), .en(decoder_2_out8), .Q(out_30), .clk(CLCK), .clr(CLR));
  Register #(.width(32), .trigger("falling")) register_26 (
    .D(P_D), .en(decoder_2_out9), .Q(out_31), .clk(CLCK), .clr(CLR));
  Register #(.width(32), .trigger("falling")) register_27 (
    .D(P_D), .en(decoder_2_out10), .Q(out_32), .clk(CLCK), .clr(CLR));
  Register #(.width(32), .trigger("falling")) register_28 (
    .D(P_D), .en(decoder_2_out11), .Q(out_33), .clk(CLCK), .clr(CLR));
  Register #(.width(32), .trigger("falling")) register_29 (
    .D(P_D), .en(decoder_2_out12), .Q(out_34), .clk(CLCK), .clr(CLR));
  Register #(.width(32), .trigger("falling")) register_30 (
    .D(P_D), .en(decoder_2_out13), .Q(out_35), .clk(CLCK), .clr(CLR));
  Register #(.width(32), .trigger("falling")) register_31 (
    .D(P_D), .en(decoder_2_out14), .Q(out_36), .clk(CLCK), .clr(CLR));
  Register #(.width(32), .trigger("falling")) register_32 (
    .D(P_D), .en(decoder_2_out15), .Q(out_37), .clk(CLCK), .clr(CLR));
  Multiplexer #(.select(5), .width(32), .enable("false")) multiplexer_1 (
    .in0(out_6), .in1(out_7), .in2(out_8), .in3(out_9), .in4(out_10), .in5(out_11), .in6(out_12),
    .in7(out_13), .in8(out_14), .in9(out_15), .in10(out_16), .in11(out_17), .in12(out_18), .in13(out_19),
    .in14(out_20), .in15(out_21), .in16(out_22), .in17(out_23), .in18(out_24), .in19(out_25), .in20(out_26),
    .in21(out_27), .in22(out_28), .in23(out_29), .in24(out_30), .in25(out_31), .in26(out_32), .in27(out_33),
    .in28(out_34), .in29(out_35), .in30(out_36), .in31(out_37), .out(multiplexer_1_out), .sel(SELECT_X));
  Shifter #(.width(32), .shift("rl")) shifter_1 (.in(multiplexer_1_out), .\dist (SELECT_Y), .out(shifter_1_out));
  Shifter #(.width(32), .shift("rr")) shifter_2 (.in({CLR_WRITE, shifter_1_out[30:0]}), .\dist (SELECT_Y), .out(P_D));

  // Other names for the same wires on the sheet: GPU_LINE0[31:0] = out_6; GPU_LINE1[31:0] = out_7;
  //   GPU_LINE2[31:0] = out_8; GPU_LINE3[31:0] = out_9; GPU_LINE4[31:0] = out_10; GPU_LINE5[31:0] = out_11;
  //   GPU_LINE6[31:0] = out_12; GPU_LINE7[31:0] = out_13; GPU_LINE8[31:0] = out_14; GPU_LINE9[31:0] = out_15;
  //   GPU_LINEA[31:0] = out_16; GPU_LINEB[31:0] = out_17; GPU_LINEC[31:0] = out_18; GPU_LINED[31:0] = out_19;
  //   GPU_LINEE[31:0] = out_20; GPU_LINEF[31:0] = out_21; SELECT[3:0] = SELECT_X[3:0]; SELECT_dw[4:0] = SELECT_X
endmodule

module GPUControl (
  input  [7:0] Data,
  input  Selected,
  input  [7:0] Function,
  input  Interrupt,
  input  CLCK,
  input  CLR,
  output CLR_SCREEN,
  output [9:0] Coords,
  output Write,
  output Pixel_value
);

  wire and_1_out, decoder_1_out0, decoder_1_out1, decoder_1_out2, decoder_1_out3, decoder_1_out4, or_4_out,
       or_5_out;
  wire [4:0] or_2_out, or_3_out;
  wire [7:0] demultiplexer_1_out0, demultiplexer_1_out1, demultiplexer_1_out2, demultiplexer_1_out3,
       demultiplexer_1_out4;

  and and_1 (and_1_out, Selected, Interrupt);
  Demultiplexer #(.select(4), .width(8), .disabled(0)) demultiplexer_1 (
    .out0(demultiplexer_1_out0), .out1(demultiplexer_1_out1), .out2(demultiplexer_1_out2),
    .out3(demultiplexer_1_out3), .out4(demultiplexer_1_out4), .in(Data), .sel(Function[3:0]), .en(Selected));  // open: out5, out6, out7, out8, out9, out10, out11, out12, out13, out14, out15
  Decoder #(.select(4), .disabled(0)) decoder_1 (
    .out0(decoder_1_out0), .out1(decoder_1_out1), .out2(decoder_1_out2), .out3(decoder_1_out3),
    .out4(decoder_1_out4), .out5(CLR_SCREEN), .sel(Function[3:0]), .en(and_1_out));  // open: out6, out7, out8, out9, out10, out11, out12, out13, out14, out15
  or or_1 (Pixel_value, demultiplexer_1_out2[7], demultiplexer_1_out3[7], demultiplexer_1_out4[7]);
  assign or_2_out = demultiplexer_1_out0[4:0] | demultiplexer_1_out3[4:0];  // OR_Gate or_2, 5 bits wide
  assign or_3_out = demultiplexer_1_out4[4:0] | demultiplexer_1_out1[4:0];  // OR_Gate or_3, 5 bits wide
  or or_4 (or_4_out, decoder_1_out0, decoder_1_out3);
  or or_5 (or_5_out, decoder_1_out1, decoder_1_out4);
  or or_6 (Write, decoder_1_out2, decoder_1_out3, decoder_1_out4);
  Register #(.width(5)) register_1 (.D(or_2_out), .en(or_4_out), .Q(Coords[9:5]), .clk(CLCK), .clr(CLR));
  Register #(.width(5)) register_2 (.D(or_3_out), .en(or_5_out), .Q(Coords[4:0]), .clk(CLCK), .clr(CLR));
endmodule

module Test (
);

  wire clock_1_out;
  wire [4:0] counter_1_q;
  wire [31:0] demultiplexer_1_out0, demultiplexer_1_out1, demultiplexer_1_out2, demultiplexer_1_out3,
       demultiplexer_1_out4, demultiplexer_1_out5, demultiplexer_1_out6, demultiplexer_1_out7,
       demultiplexer_1_out8, demultiplexer_1_out9, demultiplexer_1_out10, demultiplexer_1_out11,
       demultiplexer_1_out12, demultiplexer_1_out13, demultiplexer_1_out14, demultiplexer_1_out15,
       demultiplexer_1_out16, demultiplexer_1_out17, demultiplexer_1_out18, demultiplexer_1_out19,
       demultiplexer_1_out20, demultiplexer_1_out21, demultiplexer_1_out22, demultiplexer_1_out23,
       demultiplexer_1_out24, demultiplexer_1_out25, demultiplexer_1_out26, demultiplexer_1_out27,
       demultiplexer_1_out28, demultiplexer_1_out29, demultiplexer_1_out30, demultiplexer_1_out31,
       demultiplexer_2_out0, demultiplexer_2_out1, demultiplexer_2_out2, demultiplexer_2_out3,
       demultiplexer_2_out4, demultiplexer_2_out5, demultiplexer_2_out6, demultiplexer_2_out7,
       demultiplexer_2_out8, demultiplexer_2_out9, demultiplexer_2_out10, demultiplexer_2_out11,
       demultiplexer_2_out12, demultiplexer_2_out13, demultiplexer_2_out14, demultiplexer_2_out15,
       demultiplexer_2_out16, demultiplexer_2_out17, demultiplexer_2_out18, demultiplexer_2_out19,
       demultiplexer_2_out20, demultiplexer_2_out21, demultiplexer_2_out22, demultiplexer_2_out23,
       demultiplexer_2_out24, demultiplexer_2_out25, demultiplexer_2_out26, demultiplexer_2_out27,
       demultiplexer_2_out28, demultiplexer_2_out29, demultiplexer_2_out30, demultiplexer_2_out31,
       ram_1_data, ram_2_data;

  Clock clock_1 (.out(clock_1_out));
  Demultiplexer #(.select(5), .width(32), .disabled(0), .enable("false")) demultiplexer_1 (
    .out0(demultiplexer_1_out0), .out1(demultiplexer_1_out1), .out2(demultiplexer_1_out2),
    .out3(demultiplexer_1_out3), .out4(demultiplexer_1_out4), .out5(demultiplexer_1_out5),
    .out6(demultiplexer_1_out6), .out7(demultiplexer_1_out7), .out8(demultiplexer_1_out8),
    .out9(demultiplexer_1_out9), .out10(demultiplexer_1_out10), .out11(demultiplexer_1_out11),
    .out12(demultiplexer_1_out12), .out13(demultiplexer_1_out13), .out14(demultiplexer_1_out14),
    .out15(demultiplexer_1_out15), .out16(demultiplexer_1_out16), .out17(demultiplexer_1_out17),
    .out18(demultiplexer_1_out18), .out19(demultiplexer_1_out19), .out20(demultiplexer_1_out20),
    .out21(demultiplexer_1_out21), .out22(demultiplexer_1_out22), .out23(demultiplexer_1_out23),
    .out24(demultiplexer_1_out24), .out25(demultiplexer_1_out25), .out26(demultiplexer_1_out26),
    .out27(demultiplexer_1_out27), .out28(demultiplexer_1_out28), .out29(demultiplexer_1_out29),
    .out30(demultiplexer_1_out30), .out31(demultiplexer_1_out31), .in(ram_1_data), .sel(counter_1_q));
  RAM #(.addrWidth(5), .dataWidth(32)) ram_1 (
    .addr(counter_1_q), .data(ram_1_data), .clk(clock_1_out));  // open: sel, ld, clr
  Counter #(.width(5), .max('h1f), .trigger("falling")) counter_1 (
    .Q(counter_1_q), .clk(clock_1_out));  // open: load, D, count, carry, clr
  DotMatrix #(.inputtype("row"), .matrixcols(32), .matrixrows(32), .persist(64), .dotshape("circle")) dotmatrix_1 (
    .row0(demultiplexer_1_out0), .row1(demultiplexer_1_out1), .row2(demultiplexer_1_out2),
    .row3(demultiplexer_1_out3), .row4(demultiplexer_1_out4), .row5(demultiplexer_1_out5),
    .row6(demultiplexer_1_out6), .row7(demultiplexer_1_out7), .row8(demultiplexer_1_out8),
    .row9(demultiplexer_1_out9), .row10(demultiplexer_1_out10), .row11(demultiplexer_1_out11),
    .row12(demultiplexer_1_out12), .row13(demultiplexer_1_out13), .row14(demultiplexer_1_out14),
    .row15(demultiplexer_1_out15), .row16(demultiplexer_1_out16), .row17(demultiplexer_1_out17),
    .row18(demultiplexer_1_out18), .row19(demultiplexer_1_out19), .row20(demultiplexer_1_out20),
    .row21(demultiplexer_1_out21), .row22(demultiplexer_1_out22), .row23(demultiplexer_1_out23),
    .row24(demultiplexer_1_out24), .row25(demultiplexer_1_out25), .row26(demultiplexer_1_out26),
    .row27(demultiplexer_1_out27), .row28(demultiplexer_1_out28), .row29(demultiplexer_1_out29),
    .row30(demultiplexer_1_out30), .row31(demultiplexer_1_out31));
  DotMatrix #(.matrixcols(32), .matrixrows(32), .persist(64)) dotmatrix_2 (
    .col0(demultiplexer_2_out0), .col1(demultiplexer_2_out1), .col2(demultiplexer_2_out2),
    .col3(demultiplexer_2_out3), .col4(demultiplexer_2_out4), .col5(demultiplexer_2_out5),
    .col6(demultiplexer_2_out6), .col7(demultiplexer_2_out7), .col8(demultiplexer_2_out8),
    .col9(demultiplexer_2_out9), .col10(demultiplexer_2_out10), .col11(demultiplexer_2_out11),
    .col12(demultiplexer_2_out12), .col13(demultiplexer_2_out13), .col14(demultiplexer_2_out14),
    .col15(demultiplexer_2_out15), .col16(demultiplexer_2_out16), .col17(demultiplexer_2_out17),
    .col18(demultiplexer_2_out18), .col19(demultiplexer_2_out19), .col20(demultiplexer_2_out20),
    .col21(demultiplexer_2_out21), .col22(demultiplexer_2_out22), .col23(demultiplexer_2_out23),
    .col24(demultiplexer_2_out24), .col25(demultiplexer_2_out25), .col26(demultiplexer_2_out26),
    .col27(demultiplexer_2_out27), .col28(demultiplexer_2_out28), .col29(demultiplexer_2_out29),
    .col30(demultiplexer_2_out30), .col31(demultiplexer_2_out31));
  Demultiplexer #(.select(5), .width(32), .enable("false")) demultiplexer_2 (
    .out0(demultiplexer_2_out0), .out1(demultiplexer_2_out1), .out2(demultiplexer_2_out2),
    .out3(demultiplexer_2_out3), .out4(demultiplexer_2_out4), .out5(demultiplexer_2_out5),
    .out6(demultiplexer_2_out6), .out7(demultiplexer_2_out7), .out8(demultiplexer_2_out8),
    .out9(demultiplexer_2_out9), .out10(demultiplexer_2_out10), .out11(demultiplexer_2_out11),
    .out12(demultiplexer_2_out12), .out13(demultiplexer_2_out13), .out14(demultiplexer_2_out14),
    .out15(demultiplexer_2_out15), .out16(demultiplexer_2_out16), .out17(demultiplexer_2_out17),
    .out18(demultiplexer_2_out18), .out19(demultiplexer_2_out19), .out20(demultiplexer_2_out20),
    .out21(demultiplexer_2_out21), .out22(demultiplexer_2_out22), .out23(demultiplexer_2_out23),
    .out24(demultiplexer_2_out24), .out25(demultiplexer_2_out25), .out26(demultiplexer_2_out26),
    .out27(demultiplexer_2_out27), .out28(demultiplexer_2_out28), .out29(demultiplexer_2_out29),
    .out30(demultiplexer_2_out30), .out31(demultiplexer_2_out31), .in(ram_2_data), .sel(counter_1_q));
  RAM #(.addrWidth(5), .dataWidth(32)) ram_2 (
    .addr(counter_1_q), .data(ram_2_data), .clk(clock_1_out));  // open: sel, ld, clr
endmodule
