// Logisim project cpu_v4.circ as structural Verilog
module main (
);

  wire button_1_out, clock_1_out, clock_2_out, clock_3_out, comparator_1_eq, comparator_2_eq,
       comparator_3_eq, comparator_4_eq, comparator_5_eq, comparator_6_eq, comparator_8_eq, cpu_1_we,
       gpu_1_clearscreen, gpu_1_writeenable, or_1_out, random_1_p1, random_1_p2, rgb_video_1_p1,
       rgb_video_1_p2, s_r_ff_1_q;
  wire [2:0] pull_resistor_2_node;
  wire [3:0] priority_encoder_1_out;
  wire [4:0] joystick_1_x, joystick_1_y;
  wire [6:0] keyboard_1_data;
  wire [7:0] counter_1_q, cpu_1_data_out, divider_1_out, divider_2_out, gpu_1_xcoordinate, gpu_1_ycoordinate,
       multiplexer_1_out, ram_1_dout, subtractor_1_out, subtractor_2_out, undriven;
  wire [7:7] pull_resistor_1_node;
  wire [15:0] cpu_1_address;
  wire [23:0] gpu_1_color;

  Button button_1 (.out(button_1_out));
  RAM #(.addrWidth(16), .enables("line")) ram_1 (
    .addr(cpu_1_address), .we(cpu_1_we), .clk(clock_1_out), .din(cpu_1_data_out), .dout(ram_1_dout));
  Clock clock_1 (.out(clock_1_out));
  // Probe on cpu_1_data_out
  Clock clock_2 (.out(clock_2_out));
  Comparator #(.width(16)) comparator_1 (.a(cpu_1_address), .b(16'hff01), .eq(comparator_1_eq));  // open: gt, lt
  Comparator #(.width(16)) comparator_2 (.a(cpu_1_address), .b(16'hff80), .eq(comparator_2_eq));  // open: gt, lt
  Clock clock_3 (.out(clock_3_out));
  TTY #(.cols(68), .rows(16)) tty_1 (
    .data(cpu_1_data_out[6:0]), .clk(clock_2_out), .we(comparator_1_eq), .clr(or_1_out));
  S_R_Flip_Flop s_r_ff_1 (
    .clk(clock_3_out), .Q(s_r_ff_1_q), .preset(comparator_2_eq), .reset(comparator_3_eq));  // open: S, R, Qn
  Counter counter_1 (
    .count(s_r_ff_1_q), .Q(counter_1_q), .clk(clock_3_out), .clr(comparator_3_eq));  // open: load, D, carry, up
  CPU cpu_1 (
    .DATA_IN(multiplexer_1_out), .Reset(button_1_out), .DATA_OUT(cpu_1_data_out), .Address(cpu_1_address),
    .WE(cpu_1_we));
  // Probe on cpu_1_data_out
  // Probe on cpu_1_address
  or or_1 (or_1_out, button_1_out, comparator_8_eq);
  // Buzzer buzzer_1: pin names not known; wires that end beside it: 14'h444, s_r_ff_1_q, cpu_1_data_out[6:0]
  Comparator comparator_3 (.a(8'haa), .b(counter_1_q), .eq(comparator_3_eq));  // open: gt, lt
  // Probe on multiplexer_1_out
  Multiplexer #(.select(4), .width(8)) multiplexer_1 (
    .in0(ram_1_dout), .in1({pull_resistor_1_node[7], keyboard_1_data}), .in2(divider_1_out),
    .in3(divider_2_out), .in4(undriven), .out(multiplexer_1_out), .sel(priority_encoder_1_out));  // open: in5, in6, in7, in8, in9, in10, in11, in12, in13, in14, in15
  // Probe on {pull_resistor_1_node[7], keyboard_1_data}
  // Random random_1: pin names not known; wires that end beside it: random_1_p1, random_1_p2
  Clock clock_4 (.out(random_1_p2));
  Keyboard keyboard_1 (.clk(random_1_p2), .re(comparator_4_eq), .data(keyboard_1_data));  // open: clr, avail
  Comparator #(.width(16)) comparator_4 (.a(cpu_1_address), .b(16'hff02), .eq(comparator_4_eq));  // open: gt, lt
  Comparator #(.width(16)) comparator_5 (.a(cpu_1_address), .b(16'hff03), .eq(comparator_5_eq));  // open: gt, lt
  Comparator #(.width(16)) comparator_6 (.a(cpu_1_address), .b(16'hff04), .eq(comparator_6_eq));  // open: gt, lt
  Comparator #(.width(16)) comparator_7 (.a(cpu_1_address), .b(16'hff10), .eq(random_1_p1));  // open: gt, lt
  Comparator #(.width(16)) comparator_8 (.a(cpu_1_address), .b(16'hff05), .eq(comparator_8_eq));  // open: gt, lt
  Pull_Resistor pull_resistor_1 (.node(pull_resistor_1_node[7]));
  Priority_Encoder #(.select(4)) priority_encoder_1 (
    .in0(1'b1), .in1(comparator_4_eq), .in2(comparator_5_eq), .in3(comparator_6_eq), .in4(random_1_p1),
    .out(priority_encoder_1_out));  // open: in5, in6, in7, in8, in9, in10, in11, in12, in13, in14, in15, gs, en_out, en_in
  GPU gpu_1 (
    .Address(cpu_1_address), .DataIn(cpu_1_data_out), .Reset(button_1_out), .ClearScreen(gpu_1_clearscreen),
    .WriteEnable(gpu_1_writeenable), .XCoordinate(gpu_1_xcoordinate), .YCoordinate(gpu_1_ycoordinate),
    .Color(gpu_1_color));
  Joystick #(.bits(5)) joystick_1 (.x(joystick_1_x), .y(joystick_1_y));
  // RGB_Video #(.height(256), .width(256)) rgb_video_1: pin names not known; wires that end beside it: rgb_video_1_p1, rgb_video_1_p2, gpu_1_writeenable, gpu_1_xcoordinate, gpu_1_ycoordinate, gpu_1_color
  or or_2 (rgb_video_1_p1, button_1_out, gpu_1_clearscreen);
  Clock clock_5 (.out(rgb_video_1_p2));
  Pull_Resistor pull_resistor_2 (.node(pull_resistor_2_node));
  Subtractor subtractor_1 (
    .a({pull_resistor_2_node, joystick_1_x}), .b(8'h10), .out(subtractor_1_out));  // open: bin, bout
  Subtractor subtractor_2 (
    .a({pull_resistor_2_node, joystick_1_y}), .b(8'h10), .out(subtractor_2_out));  // open: bin, bout
  Divider #(.mode("twosComplement")) divider_1 (
    .a(subtractor_1_out), .b(8'h2), .out(divider_1_out));  // open: upper, rem
  Divider #(.mode("twosComplement")) divider_2 (
    .a(subtractor_2_out), .b(8'h2), .out(divider_2_out));  // open: upper, rem
endmodule

module CPU (
  input  [7:0] DATA_IN,
  input  Reset,
  output [7:0] DATA_OUT,
  output [15:0] Address,
  output WE
);

  wire and_1_out, clock_1_out, comparator_1_eq, comparator_2_eq, comparator_3_eq, comparator_4_eq,
       comparator_5_eq, decoder_1_out1, decoder_1_out2, decoder_1_out3, decoder_1_out4, decoder_1_out5,
       decoder_1_out6, decoder_1_out7, decoder_1_out8, decoder_1_out9, decoder_1_out10, decoder_1_out11,
       decoder_1_out12, decoder_1_out13, decoder_1_out14, demultiplexer_1_out0, demultiplexer_1_out1,
       demultiplexer_2_out0, demultiplexer_2_out1, demultiplexer_3_out0, demultiplexer_3_out1,
       demultiplexer_4_out0, demultiplexer_4_out1, demultiplexer_5_out0, demultiplexer_5_out1,
       demultiplexer_6_out0, demultiplexer_6_out1, not_1_out, or_2_out, or_3_out, PC1_carry,
       pipeline_1_offset_register, pipeline_1_pc_increment;
  wire [0:0] and_3_out;
  wire [2:0] pipeline_1_address_selector, pull_resistor_2_node;
  wire [4:0] multiplexer_1_out, multiplexer_2_out, pull_resistor_1_node;
  wire [7:0] A_q, ALU_BOTTOM, ALU_TOP, and_2_out, ARG0_q, ARG1_q_2, Arithmetic_flags, Arithmetic_result, B_q,
       C0_q, C1_q, CMP_q, D0_q, D1_q, FLAGS_q, IDX0_q, IDX1_q, multiplexer_3_out, multiplexer_4_out,
       multiplexer_5_out, multiplexer_6_out, multiplexer_7_out, multiplexer_8_out, OPCODE, PC0_q, PC1_q,
       pipeline_1_microinstruction, pull_resistor_4_node, SP0_q, SP1_q;
  wire [7:5] ARG1_q;
  wire [15:0] adder_1_out, adder_2_out, BOTTOM_WORD, multiplexer_14_out, TOP_WORD;

  or or_1 (WE, decoder_1_out1, decoder_1_out2, decoder_1_out3);
  Decoder #(.enable("false"), .select(4)) decoder_1 (
    .out1(decoder_1_out1), .out2(decoder_1_out2), .out3(decoder_1_out3), .out4(decoder_1_out4),
    .out5(decoder_1_out5), .out6(decoder_1_out6), .out7(decoder_1_out7), .out8(decoder_1_out8),
    .out9(decoder_1_out9), .out10(decoder_1_out10), .out11(decoder_1_out11), .out12(decoder_1_out12),
    .out13(decoder_1_out13), .out14(decoder_1_out14), .sel(pipeline_1_microinstruction[3:0]));  // open: out0, out15
  // Probe on pipeline_1_microinstruction[3:0]
  or or_2 (or_2_out, decoder_1_out13, decoder_1_out14);
  Demultiplexer demultiplexer_1 (
    .out0(demultiplexer_1_out0), .out1(demultiplexer_1_out1), .in(decoder_1_out6),
    .sel(pipeline_1_offset_register));
  Demultiplexer demultiplexer_2 (
    .out0(demultiplexer_2_out0), .out1(demultiplexer_2_out1), .in(decoder_1_out7),
    .sel(pipeline_1_offset_register));
  Demultiplexer #(.enable("true")) demultiplexer_3 (
    .out0(demultiplexer_3_out0), .out1(demultiplexer_3_out1), .in(decoder_1_out8),
    .sel(pipeline_1_offset_register), .en(comparator_4_eq));
  Demultiplexer demultiplexer_4 (
    .out0(demultiplexer_4_out0), .out1(demultiplexer_4_out1), .in(decoder_1_out9),
    .sel(pipeline_1_offset_register));
  Demultiplexer demultiplexer_5 (
    .out0(demultiplexer_5_out0), .out1(demultiplexer_5_out1), .in(decoder_1_out10),
    .sel(pipeline_1_offset_register));
  Demultiplexer demultiplexer_6 (
    .out0(demultiplexer_6_out0), .out1(demultiplexer_6_out1), .in(or_2_out), .sel(pipeline_1_offset_register));
  Comparator #(.mode("unsigned"), .width(4)) comparator_1 (
    .a(ARG0_q[7:4]), .b(4'b0100), .eq(comparator_1_eq));  // open: gt, lt
  Comparator #(.mode("unsigned"), .width(4)) comparator_2 (
    .a(ARG0_q[7:4]), .b(4'b0101), .eq(comparator_2_eq));  // open: gt, lt
  // Probe on DATA_OUT
  or or_3 (or_3_out, comparator_1_eq, comparator_2_eq);
  Register A (.D(DATA_OUT), .en(decoder_1_out4), .Q(A_q), .clk(clock_1_out), .clr(Reset));
  Register B (.D(DATA_OUT), .en(decoder_1_out5), .Q(B_q), .clk(clock_1_out), .clr(Reset));
  Register C0 (.D(DATA_OUT), .en(demultiplexer_1_out0), .Q(C0_q), .clk(clock_1_out), .clr(Reset));
  Register C1 (.D(DATA_OUT), .en(demultiplexer_1_out1), .Q(C1_q), .clk(clock_1_out), .clr(Reset));
  Register D0 (.D(DATA_OUT), .en(demultiplexer_2_out0), .Q(D0_q), .clk(clock_1_out), .clr(Reset));
  Register D1 (.D(DATA_OUT), .en(demultiplexer_2_out1), .Q(D1_q), .clk(clock_1_out), .clr(Reset));
  Counter PC0 (
    .load(demultiplexer_3_out0), .D(DATA_OUT), .count(and_1_out), .Q(PC0_q), .clk(clock_1_out), .clr(Reset));  // open: carry, up
  Counter PC1 (
    .load(demultiplexer_3_out1), .D(DATA_OUT), .count(pipeline_1_pc_increment), .Q(PC1_q), .carry(PC1_carry),
    .clk(clock_1_out), .clr(Reset));  // open: up
  Register SP0 (.D(DATA_OUT), .en(demultiplexer_4_out0), .Q(SP0_q), .clk(clock_1_out), .clr(Reset));
  Register SP1 (.D(DATA_OUT), .en(demultiplexer_4_out1), .Q(SP1_q), .clk(clock_1_out), .clr(Reset));
  Register IDX0 (.D(DATA_OUT), .en(demultiplexer_5_out0), .Q(IDX0_q), .clk(clock_1_out), .clr(Reset));
  Register IDX1 (.D(DATA_OUT), .en(demultiplexer_5_out1), .Q(IDX1_q), .clk(clock_1_out), .clr(Reset));
  Register u_OPCODE (.D(DATA_OUT), .en(decoder_1_out12), .Q(OPCODE), .clk(clock_1_out), .clr(Reset));
  Register ARG0 (.D(DATA_OUT), .en(demultiplexer_6_out0), .Q(ARG0_q), .clk(clock_1_out), .clr(Reset));
  Register ARG1 (.D(DATA_OUT), .en(demultiplexer_6_out1), .Q({ARG1_q, ARG1_q_2[4:0]}), .clk(clock_1_out), .clr(Reset));
  Clock clock_1 (.out(clock_1_out));
  Pull_Resistor pull_resistor_1 (.node(pull_resistor_1_node));
  Multiplexer #(.width(5)) multiplexer_1 (
    .in0(pull_resistor_1_node), .in1(ARG1_q_2[4:0]), .out(multiplexer_1_out), .sel(or_3_out));
  // Probe on DATA_IN
  // Probe on C0_q
  and and_1 (and_1_out, PC1_carry, pipeline_1_pc_increment);
  Comparator #(.width(4)) comparator_3 (
    .a(4'b1011), .b(pipeline_1_microinstruction[7:4]), .eq(comparator_3_eq));  // open: gt, lt
  Multiplexer #(.width(5)) multiplexer_2 (
    .in0(multiplexer_1_out), .in1(ARG1_q_2[4:0]), .out(multiplexer_2_out), .sel(pipeline_1_offset_register));
  Pull_Resistor pull_resistor_2 (.node(pull_resistor_2_node));
  Multiplexer #(.width(8)) multiplexer_3 (
    .in0(C0_q), .in1(C1_q), .out(multiplexer_3_out), .sel(pipeline_1_offset_register));
  Multiplexer #(.width(8)) multiplexer_4 (
    .in0(D0_q), .in1(D1_q), .out(multiplexer_4_out), .sel(pipeline_1_offset_register));
  Multiplexer #(.width(8)) multiplexer_5 (
    .in0(PC0_q), .in1(PC1_q), .out(multiplexer_5_out), .sel(pipeline_1_offset_register));
  Multiplexer #(.width(8)) multiplexer_6 (
    .in0(SP0_q), .in1(SP1_q), .out(multiplexer_6_out), .sel(pipeline_1_offset_register));
  Multiplexer #(.width(8)) multiplexer_7 (
    .in0(IDX0_q), .in1(IDX1_q), .out(multiplexer_7_out), .sel(pipeline_1_offset_register));
  Register CMP (.D(DATA_OUT), .en(decoder_1_out11), .Q(CMP_q), .clk(clock_1_out), .clr(Reset));
  assign and_2_out = CMP_q & FLAGS_q;  // AND_Gate and_2, 8 bits wide
  Register FLAGS (.D(Arithmetic_flags), .en(comparator_3_eq), .Q(FLAGS_q), .clk(clock_1_out));  // open: clr
  Multiplexer #(.width(8)) multiplexer_8 (
    .in0(ARG0_q), .in1({ARG1_q, ARG1_q_2[4:0]}), .out(multiplexer_8_out), .sel(pipeline_1_offset_register));
  Pipeline pipeline_1 (
    .OPCODE(OPCODE), .Clock(clock_1_out), .Reset(Reset), .Microinstruction(pipeline_1_microinstruction),
    .Address_Selector(pipeline_1_address_selector), .PC_INCREMENT(pipeline_1_pc_increment),
    .offset_register(pipeline_1_offset_register));
  Pull_Resistor pull_resistor_3 (.node(ARG1_q_2[7:5]));
  Comparator comparator_4 (.a(CMP_q), .b(and_2_out), .eq(comparator_4_eq));  // open: gt, lt
  ALU Arithmetic (
    .Bottom_offset(ARG0_q[3:0]), .TOP_offset(ARG0_q[7:4]), .OP({ARG1_q, ARG1_q_2[4:0]}),
    .BOTTOM_word(BOTTOM_WORD), .TOP(ALU_TOP), .BOTTOM(ALU_BOTTOM), .TOP_word(TOP_WORD),
    .REG_INC(pipeline_1_offset_register), .Destination(pipeline_1_microinstruction[3:0]),
    .RESULT(Arithmetic_result), .Flags(Arithmetic_flags));
  Multiplexer #(.select(4), .width(8)) multiplexer_9 (
    .in0({8{1'b0}}), .in1(DATA_IN), .in2(DATA_IN), .in3(DATA_IN), .in4(A_q), .in5(B_q),
    .in6(multiplexer_3_out), .in7(multiplexer_4_out), .in8(multiplexer_5_out), .in9(multiplexer_6_out),
    .in10(multiplexer_7_out), .in11(Arithmetic_result), .in12(OPCODE), .in13(multiplexer_8_out),
    .in14(multiplexer_8_out), .out(DATA_OUT), .sel(pipeline_1_microinstruction[7:4]));  // open: in15
  // Probe on pipeline_1_microinstruction[7:4]
  // Probe on pipeline_1_address_selector
  Multiplexer #(.select(4), .width(8)) multiplexer_10 (
    .in0(ARG1_q_2), .in1(DATA_IN), .in4(A_q), .in5(B_q), .in6(multiplexer_3_out), .in7(multiplexer_4_out),
    .in8(multiplexer_5_out), .in9(multiplexer_6_out), .in10(multiplexer_7_out), .in11(Arithmetic_result),
    .in12(OPCODE), .in13(multiplexer_8_out), .out(ALU_TOP), .sel(ARG0_q[7:4]));  // open: in2, in3, in14, in15
  Multiplexer #(.select(4), .width(8)) multiplexer_11 (
    .in0({pull_resistor_2_node, multiplexer_2_out}), .in1(DATA_IN), .in4(A_q), .in5(B_q),
    .in6(multiplexer_3_out), .in7(multiplexer_4_out), .in8(multiplexer_5_out), .in9(multiplexer_6_out),
    .in10(multiplexer_7_out), .in11(Arithmetic_result), .in12(OPCODE), .in13(multiplexer_8_out),
    .out(ALU_BOTTOM), .sel(ARG0_q[3:0]));  // open: in2, in3, in14, in15
  Adder #(.width(16)) adder_1 (
    .a({SP0_q, SP1_q}), .b({ARG0_q, ARG1_q, ARG1_q_2[4:0]}), .out(adder_1_out));  // open: cin, cout
  Pull_Resistor pull_resistor_4 (.node(pull_resistor_4_node));
  Adder #(.width(16)) adder_2 (
    .a({IDX0_q, IDX1_q}), .b({ARG0_q, ARG1_q, ARG1_q_2[4:0]}), .out(adder_2_out));  // open: cin, cout
  Multiplexer #(.select(4), .width(16)) multiplexer_12 (
    .in0({pull_resistor_4_node, ARG1_q_2}), .in6({C0_q, C1_q}), .in7({D0_q, D1_q}), .in8({PC0_q, PC1_q}),
    .in9({SP0_q, SP1_q}), .in10({IDX0_q, IDX1_q}), .out(TOP_WORD), .sel(ARG0_q[7:4]));  // open: in1, in2, in3, in4, in5, in11, in12, in13, in14, in15
  Multiplexer #(.select(4), .width(16)) multiplexer_13 (
    .in0({pull_resistor_4_node, ARG1_q_2}), .in6({C0_q, C1_q}), .in7({D0_q, D1_q}), .in8({PC0_q, PC1_q}),
    .in9({SP0_q, SP1_q}), .in10({IDX0_q, IDX1_q}), .out(BOTTOM_WORD), .sel(ARG0_q[3:0]));  // open: in1, in2, in3, in4, in5, in11, in12, in13, in14, in15
  Multiplexer #(.select(3), .width(16)) multiplexer_14 (
    .in0({C0_q, C1_q}), .in1({D0_q, D1_q}), .in2({PC0_q, PC1_q}), .in3(adder_1_out), .in4(adder_2_out),
    .in5({ARG0_q, ARG1_q, ARG1_q_2[4:0]}), .out(multiplexer_14_out), .sel(pipeline_1_address_selector));  // open: in6, in7
  // Probe on ARG0_q[7:4]
  // Probe on ARG0_q[3:0]
  Adder #(.width(16)) adder_3 (
    .a(multiplexer_14_out), .b({{15{1'b0}}, and_3_out[0]}), .out(Address));  // open: cin, cout
  and and_3 (and_3_out[0], pipeline_1_offset_register, not_1_out);
  not not_1 (not_1_out, comparator_5_eq);
  Comparator #(.width(3)) comparator_5 (
    .a(3'b010), .b(pipeline_1_address_selector), .eq(comparator_5_eq));  // open: gt, lt

  // Other names for the same wires on the sheet: DataBus[7:0] = DATA_OUT
endmodule

module ALU (
  input  [7:0] TOP,
  input  [7:0] BOTTOM,
  input  [7:0] OP,
  input  [3:0] TOP_offset,
  input  [3:0] Bottom_offset,
  input  [3:0] Destination,
  input  [15:0] TOP_word,
  input  [15:0] BOTTOM_word,
  input  REG_INC,
  output [7:0] RESULT,
  output [7:0] Flags
);

  wire adder_1_cout, and_1_out, and_2_out, and_5_out, comparator_3_gt, comparator_4_eq, comparator_5_eq,
       comparator_6_gt, comparator_7_lt, not_4_out, or_6_out, subtractor_1_bout, xor_2_out;
  wire [3:0] pull_resistor_1_node, pull_resistor_2_node;
  wire [3:3] and_4_out;
  wire [7:0] adder_2_out, and_3_out, comparator_1_eq, comparator_2_eq, divider_1_out, divider_1_rem,
       multiplexer_2_out, multiplexer_3_out, multiplexer_4_out, multiplexer_5_out, multiplexer_6_out,
       multiplier_1_out, multiplier_2_out, not_1_out, or_1_out, shifter_1_out, subtractor_2_out, xor_1_out;
  wire [15:0] adder_3_out, divider_2_out, divider_2_rem, multiplier_3_out, subtractor_3_out;

  // Probe on TOP
  // Probe on BOTTOM
  and and_1 (and_1_out, adder_1_cout, xor_2_out);
  Adder adder_1 (.a(BOTTOM_word[7:0]), .b(TOP_word[7:0]), .cout(adder_1_cout));  // open: out, cin
  Subtractor subtractor_1 (.a(TOP_word[7:0]), .b(BOTTOM_word[7:0]), .bout(subtractor_1_bout));  // open: out, bin
  and and_2 (and_2_out, subtractor_1_bout, xor_2_out);
  assign and_3_out = TOP & BOTTOM;  // AND_Gate and_3, 8 bits wide
  assign or_1_out = TOP | BOTTOM;  // OR_Gate or_1, 8 bits wide
  assign not_1_out = ~TOP;  // NOT_Gate not_1, 8 bits wide
  Comparator #(.mode("unsigned"), .width(16)) comparator_1 (
    .a(TOP_word), .b(BOTTOM_word), .gt(comparator_1_eq[1]), .eq(comparator_1_eq[0]), .lt(comparator_1_eq[2]));
  assign xor_1_out = TOP ^ BOTTOM;  // XOR_Gate xor_1, 8 bits wide
  Adder adder_2 (.a(TOP), .b(BOTTOM), .out(adder_2_out), .cin(and_1_out), .cout(comparator_2_eq[6]));
  Subtractor subtractor_2 (.a(TOP), .b(BOTTOM), .out(subtractor_2_out), .bin(and_2_out), .bout(comparator_2_eq[7]));
  Multiplier multiplier_1 (.a(TOP), .b(BOTTOM), .out(multiplier_1_out));  // open: cin, cout
  Divider divider_1 (.a(TOP), .b(BOTTOM), .out(divider_1_out), .rem(divider_1_rem));  // open: upper
  Multiplier #(.mode("twosComplement")) multiplier_2 (.a(TOP), .b(BOTTOM), .out(multiplier_2_out));  // open: cin, cout
  Comparator #(.mode("unsigned")) comparator_2 (
    .a(TOP), .b(BOTTOM), .gt(comparator_2_eq[1]), .eq(comparator_2_eq[0]), .lt(comparator_2_eq[2]));
  Shifter shifter_1 (.in(TOP), .\dist (BOTTOM[2:0]), .out(shifter_1_out));
  or or_2 (comparator_1_eq[5], comparator_1_eq[1], comparator_1_eq[0]);
  not not_2 (comparator_1_eq[3], comparator_1_eq[0]);
  or or_3 (comparator_1_eq[4], comparator_1_eq[0], comparator_1_eq[2]);
  Adder #(.width(16)) adder_3 (
    .a(TOP_word), .b(BOTTOM_word), .out(adder_3_out), .cout(comparator_1_eq[6]));  // open: cin
  Subtractor #(.width(16)) subtractor_3 (
    .a(TOP_word), .b(BOTTOM_word), .out(subtractor_3_out), .bout(comparator_1_eq[7]));  // open: bin
  Multiplier #(.width(16)) multiplier_3 (.a(TOP_word), .b(BOTTOM_word), .out(multiplier_3_out));  // open: cin, cout
  Divider #(.width(16)) divider_2 (
    .a(TOP_word), .b(BOTTOM_word), .out(divider_2_out), .rem(divider_2_rem));  // open: upper
  // Probe on adder_2_out
  not not_3 (comparator_2_eq[3], comparator_2_eq[0]);
  or or_4 (comparator_2_eq[5], comparator_2_eq[0], comparator_2_eq[1]);
  or or_5 (comparator_2_eq[4], comparator_2_eq[0], comparator_2_eq[2]);
  Multiplexer #(.width(8)) multiplexer_1 (.in0(comparator_2_eq), .in1(comparator_1_eq), .out(Flags));  // open: sel
  Multiplexer #(.width(8)) multiplexer_2 (
    .in0(adder_3_out[7:0]), .in1(adder_3_out[15:8]), .out(multiplexer_2_out), .sel(xor_2_out));
  Multiplexer #(.width(8)) multiplexer_3 (
    .in0(subtractor_3_out[7:0]), .in1(subtractor_3_out[15:8]), .out(multiplexer_3_out), .sel(xor_2_out));
  Multiplexer #(.width(8)) multiplexer_4 (
    .in0(multiplier_3_out[7:0]), .in1(multiplier_3_out[15:8]), .out(multiplexer_4_out), .sel(xor_2_out));
  Multiplexer #(.width(8)) multiplexer_5 (
    .in0(divider_2_out[7:0]), .in1(divider_2_out[15:8]), .out(multiplexer_5_out), .sel(xor_2_out));
  Multiplexer #(.width(8)) multiplexer_6 (
    .in0(divider_2_rem[7:0]), .in1(divider_2_rem[15:8]), .out(multiplexer_6_out), .sel(xor_2_out));
  xor xor_2 (xor_2_out, REG_INC, and_5_out);
  Comparator #(.mode("unsigned"), .width(4)) comparator_3 (
    .a({and_4_out[3], OP[7:5]}), .b(4'b1010), .gt(comparator_3_gt));  // open: eq, lt
  Multiplexer #(.select(4), .width(8)) multiplexer_7 (
    .in0(and_3_out), .in1(or_1_out), .in2(xor_1_out), .in3(not_1_out), .in4(adder_2_out),
    .in5(subtractor_2_out), .in6(multiplier_1_out), .in7(shifter_1_out), .in8(divider_1_out),
    .in9(divider_1_rem), .in10(multiplier_2_out), .in11(multiplexer_2_out), .in12(multiplexer_3_out),
    .in13(multiplexer_4_out), .in14(multiplexer_5_out), .in15(multiplexer_6_out), .out(RESULT),
    .sel({and_4_out[3], OP[7:5]}));
  and and_4 (and_4_out[3], OP[4], not_4_out);
  // Probe on RESULT
  // Probe on {and_4_out[3], OP[7:5]}
  // Probe on OP
  Pull_Resistor pull_resistor_1 (.node(pull_resistor_1_node));
  Pull_Resistor pull_resistor_2 (.node(pull_resistor_2_node));
  not not_4 (not_4_out, or_6_out);
  Comparator #(.width(4)) comparator_4 (
    .a(TOP_offset), .b(pull_resistor_1_node), .eq(comparator_4_eq));  // open: gt, lt
  Comparator #(.width(4)) comparator_5 (
    .a(Bottom_offset), .b(pull_resistor_2_node), .eq(comparator_5_eq));  // open: gt, lt
  Comparator #(.mode("unsigned"), .width(4)) comparator_6 (
    .a(Destination), .b(4'b0101), .gt(comparator_6_gt));  // open: eq, lt
  Comparator #(.mode("unsigned"), .width(4)) comparator_7 (
    .a(Destination), .b(4'b1011), .lt(comparator_7_lt));  // open: gt, eq
  or or_6 (or_6_out, comparator_4_eq, comparator_5_eq);
  and and_5 (and_5_out, comparator_6_gt, comparator_7_lt);
endmodule

module Pipeline (
  input  [7:0] OPCODE,
  input  Clock,
  input  Reset,
  output offset_register,
  output [7:0] Microinstruction,
  output PC_INCREMENT,
  output [2:0] Address_Selector
);

  wire and_1_out, and_2_out, comparator_1_gt, comparator_2_gt, comparator_3_eq, comparator_4_eq,
       comparator_5_eq, comparator_6_eq, comparator_7_eq, comparator_8_eq, or_3_out, or_5_out, t_ff_1_qn;
  wire [2:0] adder_2_out, adder_3_out, counter_1_q, DEST_ARGS_data, DEST_CYCLES_data, multiplexer_1_out,
       or_1_out, or_2_out, rom_1_data, rom_2_data, SRC_ARGS_data, SRC_CYCLES_data, subtractor_1_out;

  ROM #(.addrWidth(4), .dataWidth(3)) SRC_ARGS (.addr(OPCODE[7:4]), .data(SRC_ARGS_data));
  ROM #(.addrWidth(4), .dataWidth(3)) DEST_ARGS (.addr(OPCODE[3:0]), .data(DEST_ARGS_data));
  ROM #(.addrWidth(4), .dataWidth(3)) SRC_CYCLES (.addr(OPCODE[7:4]), .data(SRC_CYCLES_data));
  ROM #(.addrWidth(4), .dataWidth(3)) DEST_CYCLES (.addr(OPCODE[3:0]), .data(DEST_CYCLES_data));
  Adder #(.width(3)) adder_1 ();  // open: a, b, out, cin, cout
  assign or_1_out = SRC_ARGS_data | DEST_ARGS_data;  // OR_Gate or_1, 3 bits wide
  assign or_2_out = SRC_CYCLES_data | DEST_CYCLES_data;  // OR_Gate or_2, 3 bits wide
  Adder #(.width(3)) adder_2 (.a(3'b011), .b(or_2_out), .out(adder_2_out));  // open: cin, cout
  Comparator #(.width(3)) comparator_1 (.a(or_2_out), .b(3'b000), .gt(comparator_1_gt));  // open: eq, lt
  ROM #(.addrWidth(4), .dataWidth(3)) rom_1 (.addr(OPCODE[7:4]), .data(rom_1_data));
  ROM #(.addrWidth(4), .dataWidth(3)) rom_2 (.addr(OPCODE[3:0]), .data(rom_2_data));
  Comparator #(.width(3)) comparator_2 (.a(or_1_out), .b(3'b001), .gt(comparator_2_gt));  // open: eq, lt
  Comparator #(.width(3)) comparator_3 (.a(or_1_out), .b(counter_1_q), .eq(comparator_3_eq));  // open: gt, lt
  Comparator #(.width(3)) comparator_4 (.a(adder_2_out), .b(counter_1_q), .eq(comparator_4_eq));  // open: gt, lt
  Subtractor #(.width(3)) subtractor_1 (.a(3'b011), .b(or_1_out), .out(subtractor_1_out));  // open: bin, bout
  or or_3 (or_3_out, comparator_4_eq, comparator_3_eq);
  Multiplexer #(.select(3), .width(3)) multiplexer_1 (
    .in0(subtractor_1_out), .in1(3'b011), .in2(3'b011), .in3(3'b000), .in4(3'b000), .out(multiplexer_1_out),
    .sel(counter_1_q));  // open: in5, in6, in7
  and and_1 (and_1_out, comparator_2_gt, comparator_3_eq);
  or or_4 (offset_register, and_1_out, and_2_out);
  and and_2 (and_2_out, comparator_1_gt, comparator_4_eq);
  Counter #(.max('h7), .trigger("falling"), .width(3)) counter_1 (
    .load(or_3_out), .D(multiplexer_1_out), .Q(counter_1_q), .clk(Clock), .clr(Reset));  // open: count, carry, up
  Multiplexer #(.select(3), .width(8)) multiplexer_2 (
    .in0(8'h1c), .in1(8'h1d), .in2(8'h1d), .in3(OPCODE), .in4(OPCODE), .out(Microinstruction),
    .sel(counter_1_q));  // open: in5, in6, in7
  // Probe on Microinstruction
  Adder #(.width(3)) adder_3 (.a(rom_1_data), .b(rom_2_data), .out(adder_3_out));  // open: cin, cout
  Multiplexer #(.select(3), .width(3)) multiplexer_3 (
    .in0(3'b010), .in1(3'b010), .in2(3'b010), .in3(adder_3_out), .in4(adder_3_out), .out(Address_Selector),
    .sel(counter_1_q));  // open: in5, in6, in7
  Comparator #(.width(3)) comparator_5 (.a(counter_1_q), .b(3'b000), .eq(comparator_5_eq));  // open: gt, lt
  Comparator #(.width(3)) comparator_6 (.a(counter_1_q), .b(3'b001), .eq(comparator_6_eq));  // open: gt, lt
  Comparator #(.width(3)) comparator_7 (.a(counter_1_q), .b(3'b010), .eq(comparator_7_eq));  // open: gt, lt
  buf or_5 (or_5_out, comparator_8_eq);  // OR_Gate
  Comparator #(.width(3)) comparator_8 (.a(counter_1_q), .b(3'b011), .eq(comparator_8_eq));  // open: gt, lt
  or or_6 (PC_INCREMENT, comparator_5_eq, comparator_6_eq, comparator_7_eq);
  T_Flip_Flop t_ff_1 (.clk(Clock), .T(or_5_out), .Qn(t_ff_1_qn), .reset(comparator_5_eq));  // open: Q, preset

  // Notes on the sheet:
  //   contents of SRC_ARGS (hex, n*v repeats v):
  //   0 2 2 2 7*0 2 0 1 2
  //   contents of DEST_ARGS (hex, n*v repeats v):
  //   0 2 2 2 9*0 1 2
  //   contents of SRC_CYCLES (hex, n*v repeats v):
  //   6*0 5*1 4*0 1
  //   contents of DEST_CYCLES (hex, n*v repeats v):
  //   6*0 5*1 4*0 1
  //   contents of rom_1 (hex, n*v repeats v):
  //   2 5 3 4
  //   contents of rom_2 (hex, n*v repeats v):
  //   2 5 3 4
endmodule

module GPU (
  input  [15:0] Address,
  input  [7:0] DataIn,
  input  Reset,
  output ClearScreen,
  output WriteEnable,
  output [7:0] XCoordinate,
  output [7:0] YCoordinate,
  output [23:0] Color
);

  wire and_1_out, and_2_out, clock_1_out, comparator_1_gt, comparator_2_lt, comparator_3_eq, comparator_4_eq,
       comparator_5_eq, comparator_6_eq, decoder_1_out1, decoder_1_out2, decoder_1_out3, decoder_1_out4,
       decoder_1_out5, decoder_1_out6, decoder_1_out7, decoder_1_out8, or_1_out, or_2_out, s_r_ff_1_q;
  wire [7:0] Command_q, Vecx_q, VecY_q, XCoord_q, YCoord_q;

  Comparator #(.mode("unsigned"), .width(16)) comparator_1 (
    .a(Address), .b(16'hff40), .gt(comparator_1_gt));  // open: eq, lt
  and and_1 (and_1_out, comparator_1_gt, comparator_2_lt);
  Comparator #(.mode("unsigned"), .width(16)) comparator_2 (
    .a(Address), .b(16'hff4f), .lt(comparator_2_lt));  // open: gt, eq
  Decoder #(.select(4)) decoder_1 (
    .out1(decoder_1_out1), .out2(decoder_1_out2), .out3(decoder_1_out3), .out4(decoder_1_out4),
    .out5(decoder_1_out5), .out6(decoder_1_out6), .out7(decoder_1_out7), .out8(decoder_1_out8),
    .sel(Address[3:0]), .en(and_1_out));  // open: out0, out9, out10, out11, out12, out13, out14, out15
  Clock clock_1 (.out(clock_1_out));
  Register Command (.D(DataIn), .en(decoder_1_out1), .Q(Command_q), .clk(clock_1_out), .clr(or_2_out));
  Register XCoord (.D(DataIn), .en(decoder_1_out2), .Q(XCoord_q), .clk(clock_1_out), .clr(Reset));
  Register YCoord (.D(DataIn), .en(decoder_1_out3), .Q(YCoord_q), .clk(clock_1_out), .clr(Reset));
  Register Vecx (.D(DataIn), .en(decoder_1_out4), .Q(Vecx_q), .clk(clock_1_out), .clr(Reset));
  Register VecY (.D(DataIn), .en(decoder_1_out5), .Q(VecY_q), .clk(clock_1_out), .clr(Reset));
  Register RColor (.D(DataIn), .en(decoder_1_out6), .Q(Color[23:16]), .clk(clock_1_out), .clr(Reset));
  Register GColor (.D(DataIn), .en(decoder_1_out7), .Q(Color[15:8]), .clk(clock_1_out), .clr(Reset));
  Register BColor (.D(DataIn), .en(decoder_1_out8), .Q(Color[7:0]), .clk(clock_1_out), .clr(Reset));
  Comparator comparator_3 (.a(Command_q), .b(8'h2), .eq(comparator_3_eq));  // open: gt, lt
  or or_1 (or_1_out, s_r_ff_1_q, comparator_5_eq);
  Counter #(.ongoal("stay")) counter_1 (
    .load(s_r_ff_1_q), .D(YCoord_q), .count(comparator_5_eq), .Q(YCoordinate), .clk(clock_1_out), .clr(Reset));  // open: carry, up
  Comparator comparator_4 (.a(Command_q), .b(8'h1), .eq(comparator_4_eq));  // open: gt, lt
  or or_2 (or_2_out, ClearScreen, s_r_ff_1_q);
  S_R_Flip_Flop s_r_ff_1 (
    .S(comparator_3_eq), .clk(clock_1_out), .R(s_r_ff_1_q), .Q(s_r_ff_1_q));  // open: Qn, preset, reset
  Counter #(.ongoal("load")) counter_2 (
    .load(or_1_out), .D(XCoord_q), .count(WriteEnable), .Q(XCoordinate), .clk(clock_1_out), .clr(Reset));  // open: carry, up
  Comparator #(.mode("unsigned")) comparator_5 (.a(XCoordinate), .b(Vecx_q), .eq(comparator_5_eq));  // open: gt, lt
  Comparator #(.mode("unsigned")) comparator_6 (.a(YCoordinate), .b(VecY_q), .eq(comparator_6_eq));  // open: gt, lt
  S_R_Flip_Flop s_r_ff_2 (
    .S(comparator_4_eq), .clk(clock_1_out), .R(ClearScreen), .Q(ClearScreen));  // open: Qn, preset, reset
  and and_2 (and_2_out, comparator_5_eq, comparator_6_eq);
  S_R_Flip_Flop s_r_ff_3 (
    .S(s_r_ff_1_q), .R(and_2_out), .clk(clock_1_out), .Q(WriteEnable));  // open: reset, Qn, preset
endmodule
